// Logisim project ALU.circ as structural Verilog: 33 circuits, main circuit main
module HalfAdder (
  input  A,
  input  B,
  output Sum,
  output Carry
);

  and and_1 (Carry, A, B);
  xor xor_1 (Sum, A, B);
endmodule

module FullAdder (
  input  A,
  input  B,
  input  Cin,
  output Sum,
  output Cout
);

  wire halfadder_1_carry, halfadder_1_sum, halfadder_2_carry;

  HalfAdder halfadder_1 (.A(A), .B(B), .Sum(halfadder_1_sum), .Carry(halfadder_1_carry));
  HalfAdder halfadder_2 (.A(halfadder_1_sum), .B(Cin), .Sum(Sum), .Carry(halfadder_2_carry));
  or or_1 (Cout, halfadder_1_carry, halfadder_2_carry);
endmodule

module Select1bit (
  input  Sel,
  input  X,
  input  Y,
  output SelOut
);

  wire and_1_out, and_2_out, not_1_out;

  not not_1 (not_1_out, Sel);
  and and_1 (and_1_out, not_1_out, X);
  and and_2 (and_2_out, Sel, Y);
  or or_1 (SelOut, and_1_out, and_2_out);
endmodule

module Register4bit (
  input  Load,
  input  D0,
  input  D1,
  input  D2,
  input  D3,
  input  CLK,
  output Q0,
  output Q1,
  output Q2,
  output Q3
);

  wire and_1_out, and_2_out, and_3_out, and_4_out, and_5_out, and_6_out, and_7_out, and_8_out, not_1_out,
       or_1_out, or_2_out, or_3_out, or_4_out;

  or or_1 (or_1_out, and_1_out, and_2_out);
  D_Flip_Flop d_ff_1 (.D(or_1_out), .clk(CLK), .Q(Q0));  // open: Qn, preset, reset
  and and_1 (and_1_out, not_1_out, Q0);
  and and_2 (and_2_out, Load, D0);
  or or_2 (or_2_out, and_3_out, and_4_out);
  and and_3 (and_3_out, not_1_out, Q1);
  and and_4 (and_4_out, Load, D1);
  D_Flip_Flop d_ff_2 (.D(or_2_out), .clk(CLK), .Q(Q1));  // open: Qn, preset, reset
  not not_1 (not_1_out, Load);
  D_Flip_Flop d_ff_3 (.D(or_3_out), .clk(CLK), .Q(Q2));  // open: Qn, preset, reset
  and and_5 (and_5_out, Load, D2);
  and and_6 (and_6_out, not_1_out, Q2);
  D_Flip_Flop d_ff_4 (.D(or_4_out), .clk(CLK), .Q(Q3));  // open: Qn, preset, reset
  or or_3 (or_3_out, and_6_out, and_5_out);
  and and_7 (and_7_out, Load, D3);
  and and_8 (and_8_out, not_1_out, Q3);
  or or_4 (or_4_out, and_8_out, and_7_out);
endmodule

module Comparator4bitGTEQ (
  input  A3,
  input  A2,
  input  A1,
  input  A0,
  input  B3,
  input  B2,
  input  B1,
  input  B0,
  input  GTin,
  input  EQin,
  output GT,
  output EQ
);

  wire AND1_out, E0_out, E1_out, E2_out, E3_out, EQloc_out, G0_out, G1_out, G2_out, G3_out, not_1_out,
       not_2_out, not_3_out, not_4_out, or_1_out;

  not not_1 (not_1_out, B3);
  not not_2 (not_2_out, B2);
  not not_3 (not_3_out, B1);
  not not_4 (not_4_out, B0);
  xnor E3 (E3_out, A3, B3);
  xnor E2 (E2_out, A2, B2);
  xnor E1 (E1_out, A1, B1);
  xnor E0 (E0_out, A0, B0);
  and G3 (G3_out, A3, not_1_out);
  and G2 (G2_out, E3_out, A2, not_2_out);
  and G1 (G1_out, E3_out, E2_out, A1, not_3_out);
  and G0 (G0_out, E3_out, E2_out, E1_out, A0, not_4_out);
  and EQloc (EQloc_out, E3_out, E2_out, E1_out, E0_out);
  and AND1 (AND1_out, EQloc_out, GTin);
  and AND2 (EQ, EQloc_out, EQin);
  or or_1 (or_1_out, G3_out, G2_out, G1_out, G0_out);
  or OR2 (GT, or_1_out, AND1_out);
endmodule

module Adder8bit (
  input  [7:0] A,
  input  [7:0] B,
  input  Cin,
  output [7:0] S,
  output Cout,
  output V
);

  wire c1, c2, c3, c4, c5, c6, c7;

  FullAdder fulladder_1 (.A(A[0]), .B(B[0]), .Cin(Cin), .Sum(S[0]), .Cout(c1));
  FullAdder fulladder_2 (.A(A[1]), .B(B[1]), .Cin(c1), .Sum(S[1]), .Cout(c2));
  FullAdder fulladder_3 (.A(A[2]), .B(B[2]), .Cin(c2), .Sum(S[2]), .Cout(c3));
  FullAdder fulladder_4 (.A(A[3]), .B(B[3]), .Cin(c3), .Sum(S[3]), .Cout(c4));
  FullAdder fulladder_5 (.A(A[4]), .B(B[4]), .Cin(c4), .Sum(S[4]), .Cout(c5));
  FullAdder fulladder_6 (.A(A[5]), .B(B[5]), .Cin(c5), .Sum(S[5]), .Cout(c6));
  FullAdder fulladder_7 (.A(A[6]), .B(B[6]), .Cin(c6), .Sum(S[6]), .Cout(c7));
  FullAdder fulladder_8 (.A(A[7]), .B(B[7]), .Cin(c7), .Sum(S[7]), .Cout(Cout));
  xor xor_1 (V, c7, Cout);
endmodule

module Subtractor8bit (
  input  [7:0] A,
  input  [7:0] B,
  output [7:0] S,
  output Cout,
  output V
);

  wire [7:0] nB;

  not not_1 (nB[0], B[0]);
  not not_2 (nB[1], B[1]);
  not not_3 (nB[2], B[2]);
  not not_4 (nB[3], B[3]);
  not not_5 (nB[4], B[4]);
  not not_6 (nB[5], B[5]);
  not not_7 (nB[6], B[6]);
  not not_8 (nB[7], B[7]);
  Adder8bit adder8bit_1 (.A(A), .B(nB), .Cin(1'b1), .S(S), .Cout(Cout), .V(V));
endmodule

module INC8bit (
  input  [7:0] A,
  output [7:0] S,
  output Cout,
  output V
);

  Adder8bit adder8bit_1 (.A(A), .B({8{1'b0}}), .Cin(1'b1), .S(S), .Cout(Cout), .V(V));
endmodule

module DEC8bit (
  input  [7:0] A,
  output [7:0] S,
  output Cout,
  output V
);

  Adder8bit adder8bit_1 (.A(A), .B({8{1'b1}}), .Cin(1'b0), .S(S), .Cout(Cout), .V(V));
endmodule

module Register8bit (
  input  Load,
  input  [7:0] D,
  input  CLK,
  output [7:0] Q
);

  Register4bit register4bit_1 (
    .Load(Load), .D0(D[0]), .D1(D[1]), .D2(D[2]), .D3(D[3]), .CLK(CLK), .Q0(Q[0]), .Q1(Q[1]), .Q2(Q[2]),
    .Q3(Q[3]));
  Register4bit register4bit_2 (
    .Load(Load), .D0(D[4]), .D1(D[5]), .D2(D[6]), .D3(D[7]), .CLK(CLK), .Q0(Q[4]), .Q1(Q[5]), .Q2(Q[6]),
    .Q3(Q[7]));
endmodule

module LogicUnit8 (
  input  [7:0] A,
  input  [7:0] B,
  output [7:0] And,
  output [7:0] Or,
  output [7:0] Xor,
  output [7:0] NotA
);

  and and_1 (And[0], A[0], B[0]);
  and and_2 (And[1], A[1], B[1]);
  and and_3 (And[2], A[2], B[2]);
  and and_4 (And[3], A[3], B[3]);
  and and_5 (And[4], A[4], B[4]);
  and and_6 (And[5], A[5], B[5]);
  and and_7 (And[6], A[6], B[6]);
  and and_8 (And[7], A[7], B[7]);
  or or_1 (Or[0], A[0], B[0]);
  or or_2 (Or[1], A[1], B[1]);
  or or_3 (Or[2], A[2], B[2]);
  or or_4 (Or[3], A[3], B[3]);
  or or_5 (Or[4], A[4], B[4]);
  or or_6 (Or[5], A[5], B[5]);
  or or_7 (Or[6], A[6], B[6]);
  or or_8 (Or[7], A[7], B[7]);
  xor xor_1 (Xor[0], A[0], B[0]);
  xor xor_2 (Xor[1], A[1], B[1]);
  xor xor_3 (Xor[2], A[2], B[2]);
  xor xor_4 (Xor[3], A[3], B[3]);
  xor xor_5 (Xor[4], A[4], B[4]);
  xor xor_6 (Xor[5], A[5], B[5]);
  xor xor_7 (Xor[6], A[6], B[6]);
  xor xor_8 (Xor[7], A[7], B[7]);
  not not_1 (NotA[0], A[0]);
  not not_2 (NotA[1], A[1]);
  not not_3 (NotA[2], A[2]);
  not not_4 (NotA[3], A[3]);
  not not_5 (NotA[4], A[4]);
  not not_6 (NotA[5], A[5]);
  not not_7 (NotA[6], A[6]);
  not not_8 (NotA[7], A[7]);

  // Other names for the same wires on the sheet: not0 = NotA[0]; not1 = NotA[1]; not2 = NotA[2]; not3 = NotA[3];
  //   not4 = NotA[4]; not5 = NotA[5]; not6 = NotA[6]; not7 = NotA[7]
endmodule

module Select8bit (
  input  Sel,
  input  [7:0] X,
  input  [7:0] Y,
  output [7:0] Out
);

  Select1bit select1bit_1 (.Sel(Sel), .X(X[0]), .Y(Y[0]), .SelOut(Out[0]));
  Select1bit select1bit_2 (.Sel(Sel), .X(X[1]), .Y(Y[1]), .SelOut(Out[1]));
  Select1bit select1bit_3 (.Sel(Sel), .X(X[2]), .Y(Y[2]), .SelOut(Out[2]));
  Select1bit select1bit_4 (.Sel(Sel), .X(X[3]), .Y(Y[3]), .SelOut(Out[3]));
  Select1bit select1bit_5 (.Sel(Sel), .X(X[4]), .Y(Y[4]), .SelOut(Out[4]));
  Select1bit select1bit_6 (.Sel(Sel), .X(X[5]), .Y(Y[5]), .SelOut(Out[5]));
  Select1bit select1bit_7 (.Sel(Sel), .X(X[6]), .Y(Y[6]), .SelOut(Out[6]));
  Select1bit select1bit_8 (.Sel(Sel), .X(X[7]), .Y(Y[7]), .SelOut(Out[7]));

  // Other names for the same wires on the sheet: o0 = Out[0]; o1 = Out[1]; o2 = Out[2]; o3 = Out[3]; o4 = Out[4];
  //   o5 = Out[5]; o6 = Out[6]; o7 = Out[7]
endmodule

module Comparator8bit (
  input  [7:0] A,
  input  [7:0] B,
  output GT,
  output EQ,
  output GTE
);

  wire eql, gtl;

  Comparator4bitGTEQ comparator4bitgteq_1 (
    .A3(A[3]), .A2(A[2]), .A1(A[1]), .A0(A[0]), .B3(B[3]), .B2(B[2]), .B1(B[1]), .B0(B[0]), .GTin(1'b0),
    .EQin(1'b1), .GT(gtl), .EQ(eql));
  Comparator4bitGTEQ comparator4bitgteq_2 (
    .A3(A[7]), .A2(A[6]), .A1(A[5]), .A0(A[4]), .B3(B[7]), .B2(B[6]), .B1(B[5]), .B0(B[4]), .GTin(gtl),
    .EQin(eql), .GT(GT), .EQ(EQ));
  or or_1 (GTE, GT, EQ);
endmodule

module ZeroDetect8 (
  input  [7:0] In,
  output Z
);

  nor nor_1 (Z, In[0], In[1], In[2], In[3], In[4], In[5], In[6], In[7]);

  // Other names for the same wires on the sheet: i0 = In[0]; i1 = In[1]; i2 = In[2]; i3 = In[3]; i4 = In[4];
  //   i5 = In[5]; i6 = In[6]; i7 = In[7]
endmodule

module OpMux16x8 (
  input  [3:0] Sel,
  input  [7:0] In0,
  input  [7:0] In1,
  input  [7:0] In2,
  input  [7:0] In3,
  input  [7:0] In4,
  input  [7:0] In5,
  input  [7:0] In6,
  input  [7:0] In7,
  input  [7:0] In8,
  input  [7:0] In9,
  input  [7:0] In10,
  input  [7:0] In11,
  input  [7:0] In12,
  input  [7:0] In13,
  input  [7:0] In14,
  input  [7:0] In15,
  output [7:0] Out
);

  wire d0, d1, d2, d3, d4, d5, d6, d7, d8, d9, d10, d11, d12, d13, d14, d15, ns0, ns1, ns2, ns3, t0_0, t0_1,
       t0_2, t0_3, t0_4, t0_5, t0_6, t0_7, t0_8, t0_9, t0_10, t0_11, t0_12, t0_13, t0_14, t0_15, t1_0, t1_1,
       t1_2, t1_3, t1_4, t1_5, t1_6, t1_7, t1_8, t1_9, t1_10, t1_11, t1_12, t1_13, t1_14, t1_15, t2_0, t2_1,
       t2_2, t2_3, t2_4, t2_5, t2_6, t2_7, t2_8, t2_9, t2_10, t2_11, t2_12, t2_13, t2_14, t2_15, t3_0, t3_1,
       t3_2, t3_3, t3_4, t3_5, t3_6, t3_7, t3_8, t3_9, t3_10, t3_11, t3_12, t3_13, t3_14, t3_15, t4_0, t4_1,
       t4_2, t4_3, t4_4, t4_5, t4_6, t4_7, t4_8, t4_9, t4_10, t4_11, t4_12, t4_13, t4_14, t4_15, t5_0, t5_1,
       t5_2, t5_3, t5_4, t5_5, t5_6, t5_7, t5_8, t5_9, t5_10, t5_11, t5_12, t5_13, t5_14, t5_15, t6_0, t6_1,
       t6_2, t6_3, t6_4, t6_5, t6_6, t6_7, t6_8, t6_9, t6_10, t6_11, t6_12, t6_13, t6_14, t6_15, t7_0, t7_1,
       t7_2, t7_3, t7_4, t7_5, t7_6, t7_7, t7_8, t7_9, t7_10, t7_11, t7_12, t7_13, t7_14, t7_15;

  not not_1 (ns0, Sel[0]);
  not not_2 (ns1, Sel[1]);
  not not_3 (ns2, Sel[2]);
  not not_4 (ns3, Sel[3]);
  and and_1 (d0, ns0, ns1, ns2, ns3);
  and and_2 (d1, Sel[0], ns1, ns2, ns3);
  and and_3 (d2, ns0, Sel[1], ns2, ns3);
  and and_4 (d3, Sel[0], Sel[1], ns2, ns3);
  and and_5 (d4, ns0, ns1, Sel[2], ns3);
  and and_6 (d5, Sel[0], ns1, Sel[2], ns3);
  and and_7 (d6, ns0, Sel[1], Sel[2], ns3);
  and and_8 (d7, Sel[0], Sel[1], Sel[2], ns3);
  and and_9 (d8, ns0, ns1, ns2, Sel[3]);
  and and_10 (d9, Sel[0], ns1, ns2, Sel[3]);
  and and_11 (d10, ns0, Sel[1], ns2, Sel[3]);
  and and_12 (d11, Sel[0], Sel[1], ns2, Sel[3]);
  and and_13 (d12, ns0, ns1, Sel[2], Sel[3]);
  and and_14 (d13, Sel[0], ns1, Sel[2], Sel[3]);
  and and_15 (d14, ns0, Sel[1], Sel[2], Sel[3]);
  and and_16 (d15, Sel[0], Sel[1], Sel[2], Sel[3]);
  and and_17 (t0_0, d0, In0[0]);
  and and_18 (t0_1, d1, In1[0]);
  and and_19 (t0_2, d2, In2[0]);
  and and_20 (t0_3, d3, In3[0]);
  and and_21 (t0_4, d4, In4[0]);
  and and_22 (t0_5, d5, In5[0]);
  and and_23 (t0_6, d6, In6[0]);
  and and_24 (t0_7, d7, In7[0]);
  and and_25 (t0_8, d8, In8[0]);
  and and_26 (t0_9, d9, In9[0]);
  and and_27 (t0_10, d10, In10[0]);
  and and_28 (t0_11, d11, In11[0]);
  and and_29 (t0_12, d12, In12[0]);
  and and_30 (t0_13, d13, In13[0]);
  and and_31 (t0_14, d14, In14[0]);
  and and_32 (t0_15, d15, In15[0]);
  and and_33 (t1_0, d0, In0[1]);
  and and_34 (t1_1, d1, In1[1]);
  and and_35 (t1_2, d2, In2[1]);
  and and_36 (t1_3, d3, In3[1]);
  and and_37 (t1_4, d4, In4[1]);
  and and_38 (t1_5, d5, In5[1]);
  and and_39 (t1_6, d6, In6[1]);
  and and_40 (t1_7, d7, In7[1]);
  and and_41 (t1_8, d8, In8[1]);
  and and_42 (t1_9, d9, In9[1]);
  and and_43 (t1_10, d10, In10[1]);
  and and_44 (t1_11, d11, In11[1]);
  and and_45 (t1_12, d12, In12[1]);
  and and_46 (t1_13, d13, In13[1]);
  and and_47 (t1_14, d14, In14[1]);
  and and_48 (t1_15, d15, In15[1]);
  and and_49 (t2_0, d0, In0[2]);
  and and_50 (t2_1, d1, In1[2]);
  and and_51 (t2_2, d2, In2[2]);
  and and_52 (t2_3, d3, In3[2]);
  and and_53 (t2_4, d4, In4[2]);
  and and_54 (t2_5, d5, In5[2]);
  and and_55 (t2_6, d6, In6[2]);
  and and_56 (t2_7, d7, In7[2]);
  and and_57 (t2_8, d8, In8[2]);
  and and_58 (t2_9, d9, In9[2]);
  and and_59 (t2_10, d10, In10[2]);
  and and_60 (t2_11, d11, In11[2]);
  and and_61 (t2_12, d12, In12[2]);
  and and_62 (t2_13, d13, In13[2]);
  and and_63 (t2_14, d14, In14[2]);
  and and_64 (t2_15, d15, In15[2]);
  and and_65 (t3_0, d0, In0[3]);
  and and_66 (t3_1, d1, In1[3]);
  and and_67 (t3_2, d2, In2[3]);
  and and_68 (t3_3, d3, In3[3]);
  and and_69 (t3_4, d4, In4[3]);
  and and_70 (t3_5, d5, In5[3]);
  and and_71 (t3_6, d6, In6[3]);
  and and_72 (t3_7, d7, In7[3]);
  and and_73 (t3_8, d8, In8[3]);
  and and_74 (t3_9, d9, In9[3]);
  and and_75 (t3_10, d10, In10[3]);
  and and_76 (t3_11, d11, In11[3]);
  and and_77 (t3_12, d12, In12[3]);
  and and_78 (t3_13, d13, In13[3]);
  and and_79 (t3_14, d14, In14[3]);
  and and_80 (t3_15, d15, In15[3]);
  and and_81 (t4_0, d0, In0[4]);
  and and_82 (t4_1, d1, In1[4]);
  and and_83 (t4_2, d2, In2[4]);
  and and_84 (t4_3, d3, In3[4]);
  and and_85 (t4_4, d4, In4[4]);
  and and_86 (t4_5, d5, In5[4]);
  and and_87 (t4_6, d6, In6[4]);
  and and_88 (t4_7, d7, In7[4]);
  and and_89 (t4_8, d8, In8[4]);
  and and_90 (t4_9, d9, In9[4]);
  and and_91 (t4_10, d10, In10[4]);
  and and_92 (t4_11, d11, In11[4]);
  and and_93 (t4_12, d12, In12[4]);
  and and_94 (t4_13, d13, In13[4]);
  and and_95 (t4_14, d14, In14[4]);
  and and_96 (t4_15, d15, In15[4]);
  and and_97 (t5_0, d0, In0[5]);
  and and_98 (t5_1, d1, In1[5]);
  and and_99 (t5_2, d2, In2[5]);
  and and_100 (t5_3, d3, In3[5]);
  and and_101 (t5_4, d4, In4[5]);
  and and_102 (t5_5, d5, In5[5]);
  and and_103 (t5_6, d6, In6[5]);
  and and_104 (t5_7, d7, In7[5]);
  and and_105 (t5_8, d8, In8[5]);
  and and_106 (t5_9, d9, In9[5]);
  and and_107 (t5_10, d10, In10[5]);
  and and_108 (t5_11, d11, In11[5]);
  and and_109 (t5_12, d12, In12[5]);
  and and_110 (t5_13, d13, In13[5]);
  and and_111 (t5_14, d14, In14[5]);
  and and_112 (t5_15, d15, In15[5]);
  and and_113 (t6_0, d0, In0[6]);
  and and_114 (t6_1, d1, In1[6]);
  and and_115 (t6_2, d2, In2[6]);
  and and_116 (t6_3, d3, In3[6]);
  and and_117 (t6_4, d4, In4[6]);
  and and_118 (t6_5, d5, In5[6]);
  and and_119 (t6_6, d6, In6[6]);
  and and_120 (t6_7, d7, In7[6]);
  and and_121 (t6_8, d8, In8[6]);
  and and_122 (t6_9, d9, In9[6]);
  and and_123 (t6_10, d10, In10[6]);
  and and_124 (t6_11, d11, In11[6]);
  and and_125 (t6_12, d12, In12[6]);
  and and_126 (t6_13, d13, In13[6]);
  and and_127 (t6_14, d14, In14[6]);
  and and_128 (t6_15, d15, In15[6]);
  and and_129 (t7_0, d0, In0[7]);
  and and_130 (t7_1, d1, In1[7]);
  and and_131 (t7_2, d2, In2[7]);
  and and_132 (t7_3, d3, In3[7]);
  and and_133 (t7_4, d4, In4[7]);
  and and_134 (t7_5, d5, In5[7]);
  and and_135 (t7_6, d6, In6[7]);
  and and_136 (t7_7, d7, In7[7]);
  and and_137 (t7_8, d8, In8[7]);
  and and_138 (t7_9, d9, In9[7]);
  and and_139 (t7_10, d10, In10[7]);
  and and_140 (t7_11, d11, In11[7]);
  and and_141 (t7_12, d12, In12[7]);
  and and_142 (t7_13, d13, In13[7]);
  and and_143 (t7_14, d14, In14[7]);
  and and_144 (t7_15, d15, In15[7]);
  or or_1 (Out[0], t0_0, t0_1, t0_2, t0_3, t0_4, t0_5, t0_6, t0_7, t0_8, t0_9, t0_10, t0_11, t0_12, t0_13, t0_14, t0_15);
  or or_2 (Out[1], t1_0, t1_1, t1_2, t1_3, t1_4, t1_5, t1_6, t1_7, t1_8, t1_9, t1_10, t1_11, t1_12, t1_13, t1_14, t1_15);
  or or_3 (Out[2], t2_0, t2_1, t2_2, t2_3, t2_4, t2_5, t2_6, t2_7, t2_8, t2_9, t2_10, t2_11, t2_12, t2_13, t2_14, t2_15);
  or or_4 (Out[3], t3_0, t3_1, t3_2, t3_3, t3_4, t3_5, t3_6, t3_7, t3_8, t3_9, t3_10, t3_11, t3_12, t3_13, t3_14, t3_15);
  or or_5 (Out[4], t4_0, t4_1, t4_2, t4_3, t4_4, t4_5, t4_6, t4_7, t4_8, t4_9, t4_10, t4_11, t4_12, t4_13, t4_14, t4_15);
  or or_6 (Out[5], t5_0, t5_1, t5_2, t5_3, t5_4, t5_5, t5_6, t5_7, t5_8, t5_9, t5_10, t5_11, t5_12, t5_13, t5_14, t5_15);
  or or_7 (Out[6], t6_0, t6_1, t6_2, t6_3, t6_4, t6_5, t6_6, t6_7, t6_8, t6_9, t6_10, t6_11, t6_12, t6_13, t6_14, t6_15);
  or or_8 (Out[7], t7_0, t7_1, t7_2, t7_3, t7_4, t7_5, t7_6, t7_7, t7_8, t7_9, t7_10, t7_11, t7_12, t7_13, t7_14, t7_15);

  // Other names for the same wires on the sheet: in0_0 = In0[0]; in0_1 = In0[1]; in0_2 = In0[2]; in0_3 = In0[3];
  //   in0_4 = In0[4]; in0_5 = In0[5]; in0_6 = In0[6]; in0_7 = In0[7]; in1_0 = In1[0]; in1_1 = In1[1]; in1_2 = In1[2];
  //   in1_3 = In1[3]; in1_4 = In1[4]; in1_5 = In1[5]; in1_6 = In1[6]; in1_7 = In1[7]; in2_0 = In2[0]; in2_1 = In2[1];
  //   in2_2 = In2[2]; in2_3 = In2[3]; in2_4 = In2[4]; in2_5 = In2[5]; in2_6 = In2[6]; in2_7 = In2[7]; in3_0 = In3[0];
  //   in3_1 = In3[1]; in3_2 = In3[2]; in3_3 = In3[3]; in3_4 = In3[4]; in3_5 = In3[5]; in3_6 = In3[6]; in3_7 = In3[7];
  //   in4_0 = In4[0]; in4_1 = In4[1]; in4_2 = In4[2]; in4_3 = In4[3]; in4_4 = In4[4]; in4_5 = In4[5]; in4_6 = In4[6];
  //   in4_7 = In4[7]; in5_0 = In5[0]; in5_1 = In5[1]; in5_2 = In5[2]; in5_3 = In5[3]; in5_4 = In5[4]; in5_5 = In5[5];
  //   in5_6 = In5[6]; in5_7 = In5[7]; in6_0 = In6[0]; in6_1 = In6[1]; in6_2 = In6[2]; in6_3 = In6[3]; in6_4 = In6[4];
  //   in6_5 = In6[5]; in6_6 = In6[6]; in6_7 = In6[7]; in7_0 = In7[0]; in7_1 = In7[1]; in7_2 = In7[2]; in7_3 = In7[3];
  //   in7_4 = In7[4]; in7_5 = In7[5]; in7_6 = In7[6]; in7_7 = In7[7]; in8_0 = In8[0]; in8_1 = In8[1]; in8_2 = In8[2];
  //   in8_3 = In8[3]; in8_4 = In8[4]; in8_5 = In8[5]; in8_6 = In8[6]; in8_7 = In8[7]; in9_0 = In9[0]; in9_1 = In9[1];
  //   in9_2 = In9[2]; in9_3 = In9[3]; in9_4 = In9[4]; in9_5 = In9[5]; in9_6 = In9[6]; in9_7 = In9[7];
  //   in10_0 = In10[0]; in10_1 = In10[1]; in10_2 = In10[2]; in10_3 = In10[3]; in10_4 = In10[4]; in10_5 = In10[5];
  //   in10_6 = In10[6]; in10_7 = In10[7]; in11_0 = In11[0]; in11_1 = In11[1]; in11_2 = In11[2]; in11_3 = In11[3];
  //   in11_4 = In11[4]; in11_5 = In11[5]; in11_6 = In11[6]; in11_7 = In11[7]; in12_0 = In12[0]; in12_1 = In12[1];
  //   in12_2 = In12[2]; in12_3 = In12[3]; in12_4 = In12[4]; in12_5 = In12[5]; in12_6 = In12[6]; in12_7 = In12[7];
  //   in13_0 = In13[0]; in13_1 = In13[1]; in13_2 = In13[2]; in13_3 = In13[3]; in13_4 = In13[4]; in13_5 = In13[5];
  //   in13_6 = In13[6]; in13_7 = In13[7]; in14_0 = In14[0]; in14_1 = In14[1]; in14_2 = In14[2]; in14_3 = In14[3];
  //   in14_4 = In14[4]; in14_5 = In14[5]; in14_6 = In14[6]; in14_7 = In14[7]; in15_0 = In15[0]; in15_1 = In15[1];
  //   in15_2 = In15[2]; in15_3 = In15[3]; in15_4 = In15[4]; in15_5 = In15[5]; in15_6 = In15[6]; in15_7 = In15[7];
  //   o0 = Out[0]; o1 = Out[1]; o2 = Out[2]; o3 = Out[3]; o4 = Out[4]; o5 = Out[5]; o6 = Out[6]; o7 = Out[7];
  //   s0 = Sel[0]; s1 = Sel[1]; s2 = Sel[2]; s3 = Sel[3]
endmodule

module OpMux16x2 (
  input  [3:0] Sel,
  input  [1:0] In0,
  input  [1:0] In1,
  input  [1:0] In2,
  input  [1:0] In3,
  input  [1:0] In4,
  input  [1:0] In5,
  input  [1:0] In6,
  input  [1:0] In7,
  input  [1:0] In8,
  input  [1:0] In9,
  input  [1:0] In10,
  input  [1:0] In11,
  input  [1:0] In12,
  input  [1:0] In13,
  input  [1:0] In14,
  input  [1:0] In15,
  output [1:0] Out
);

  wire d0, d1, d2, d3, d4, d5, d6, d7, d8, d9, d10, d11, d12, d13, d14, d15, ns0, ns1, ns2, ns3, t0_0, t0_1,
       t0_2, t0_3, t0_4, t0_5, t0_6, t0_7, t0_8, t0_9, t0_10, t0_11, t0_12, t0_13, t0_14, t0_15, t1_0, t1_1,
       t1_2, t1_3, t1_4, t1_5, t1_6, t1_7, t1_8, t1_9, t1_10, t1_11, t1_12, t1_13, t1_14, t1_15;

  not not_1 (ns0, Sel[0]);
  not not_2 (ns1, Sel[1]);
  not not_3 (ns2, Sel[2]);
  not not_4 (ns3, Sel[3]);
  and and_1 (d0, ns0, ns1, ns2, ns3);
  and and_2 (d1, Sel[0], ns1, ns2, ns3);
  and and_3 (d2, ns0, Sel[1], ns2, ns3);
  and and_4 (d3, Sel[0], Sel[1], ns2, ns3);
  and and_5 (d4, ns0, ns1, Sel[2], ns3);
  and and_6 (d5, Sel[0], ns1, Sel[2], ns3);
  and and_7 (d6, ns0, Sel[1], Sel[2], ns3);
  and and_8 (d7, Sel[0], Sel[1], Sel[2], ns3);
  and and_9 (d8, ns0, ns1, ns2, Sel[3]);
  and and_10 (d9, Sel[0], ns1, ns2, Sel[3]);
  and and_11 (d10, ns0, Sel[1], ns2, Sel[3]);
  and and_12 (d11, Sel[0], Sel[1], ns2, Sel[3]);
  and and_13 (d12, ns0, ns1, Sel[2], Sel[3]);
  and and_14 (d13, Sel[0], ns1, Sel[2], Sel[3]);
  and and_15 (d14, ns0, Sel[1], Sel[2], Sel[3]);
  and and_16 (d15, Sel[0], Sel[1], Sel[2], Sel[3]);
  and and_17 (t0_0, d0, In0[0]);
  and and_18 (t0_1, d1, In1[0]);
  and and_19 (t0_2, d2, In2[0]);
  and and_20 (t0_3, d3, In3[0]);
  and and_21 (t0_4, d4, In4[0]);
  and and_22 (t0_5, d5, In5[0]);
  and and_23 (t0_6, d6, In6[0]);
  and and_24 (t0_7, d7, In7[0]);
  and and_25 (t0_8, d8, In8[0]);
  and and_26 (t0_9, d9, In9[0]);
  and and_27 (t0_10, d10, In10[0]);
  and and_28 (t0_11, d11, In11[0]);
  and and_29 (t0_12, d12, In12[0]);
  and and_30 (t0_13, d13, In13[0]);
  and and_31 (t0_14, d14, In14[0]);
  and and_32 (t0_15, d15, In15[0]);
  and and_33 (t1_0, d0, In0[1]);
  and and_34 (t1_1, d1, In1[1]);
  and and_35 (t1_2, d2, In2[1]);
  and and_36 (t1_3, d3, In3[1]);
  and and_37 (t1_4, d4, In4[1]);
  and and_38 (t1_5, d5, In5[1]);
  and and_39 (t1_6, d6, In6[1]);
  and and_40 (t1_7, d7, In7[1]);
  and and_41 (t1_8, d8, In8[1]);
  and and_42 (t1_9, d9, In9[1]);
  and and_43 (t1_10, d10, In10[1]);
  and and_44 (t1_11, d11, In11[1]);
  and and_45 (t1_12, d12, In12[1]);
  and and_46 (t1_13, d13, In13[1]);
  and and_47 (t1_14, d14, In14[1]);
  and and_48 (t1_15, d15, In15[1]);
  or or_1 (Out[0], t0_0, t0_1, t0_2, t0_3, t0_4, t0_5, t0_6, t0_7, t0_8, t0_9, t0_10, t0_11, t0_12, t0_13, t0_14, t0_15);
  or or_2 (Out[1], t1_0, t1_1, t1_2, t1_3, t1_4, t1_5, t1_6, t1_7, t1_8, t1_9, t1_10, t1_11, t1_12, t1_13, t1_14, t1_15);

  // Other names for the same wires on the sheet: in0_0 = In0[0]; in0_1 = In0[1]; in1_0 = In1[0]; in1_1 = In1[1];
  //   in2_0 = In2[0]; in2_1 = In2[1]; in3_0 = In3[0]; in3_1 = In3[1]; in4_0 = In4[0]; in4_1 = In4[1]; in5_0 = In5[0];
  //   in5_1 = In5[1]; in6_0 = In6[0]; in6_1 = In6[1]; in7_0 = In7[0]; in7_1 = In7[1]; in8_0 = In8[0]; in8_1 = In8[1];
  //   in9_0 = In9[0]; in9_1 = In9[1]; in10_0 = In10[0]; in10_1 = In10[1]; in11_0 = In11[0]; in11_1 = In11[1];
  //   in12_0 = In12[0]; in12_1 = In12[1]; in13_0 = In13[0]; in13_1 = In13[1]; in14_0 = In14[0]; in14_1 = In14[1];
  //   in15_0 = In15[0]; in15_1 = In15[1]; o0 = Out[0]; o1 = Out[1]; s0 = Sel[0]; s1 = Sel[1]; s2 = Sel[2];
  //   s3 = Sel[3]
endmodule

module DivStep8 (
  input  [7:0] R,
  input  [7:0] B,
  input  [7:0] Qin,
  output [7:0] N,
  output [7:0] Qout
);

  wire bnz, gte;
  wire [7:0] diff;

  or or_1 (bnz, B[0], B[1], B[2], B[3], B[4], B[5], B[6], B[7]);
  Comparator8bit comparator8bit_1 (.A(R), .B(B), .GTE(gte));  // open: GT, EQ
  Subtractor8bit subtractor8bit_1 (.A(R), .B(B), .S(diff));  // open: Cout, V
  and and_1 (Qout[0], gte, bnz);
  Select8bit select8bit_1 (.Sel(Qout[0]), .X(R), .Y(diff), .Out(N));

  assign Qout[7:1] = Qin[6:0];

  // Other names for the same wires on the sheet: q = Qout[0]; qi0 = Qin[0]; qi1 = Qin[1]; qi2 = Qin[2]; qi3 = Qin[3];
  //   qi4 = Qin[4]; qi5 = Qin[5]; qi6 = Qin[6]
endmodule

module DIV8bit (
  input  [7:0] A,
  input  [7:0] B,
  output [7:0] Q,
  output [7:0] R,
  output DZ
);

  wire [7:0] n0, n1, n2, n3, n4, n5, n6, q0, q1, q2, q3, q4, q5, q6;

  ZeroDetect8 zerodetect8_1 (.In(B), .Z(DZ));
  DivStep8 divstep8_1 (.R({{7{1'b0}}, A[7]}), .B(B), .Qin({8{1'b0}}), .N(n0), .Qout(q0));
  DivStep8 divstep8_2 (.R({n0[6:0], A[6]}), .B(B), .Qin(q0), .N(n1), .Qout(q1));
  DivStep8 divstep8_3 (.R({n1[6:0], A[5]}), .B(B), .Qin(q1), .N(n2), .Qout(q2));
  DivStep8 divstep8_4 (.R({n2[6:0], A[4]}), .B(B), .Qin(q2), .N(n3), .Qout(q3));
  DivStep8 divstep8_5 (.R({n3[6:0], A[3]}), .B(B), .Qin(q3), .N(n4), .Qout(q4));
  DivStep8 divstep8_6 (.R({n4[6:0], A[2]}), .B(B), .Qin(q4), .N(n5), .Qout(q5));
  DivStep8 divstep8_7 (.R({n5[6:0], A[1]}), .B(B), .Qin(q5), .N(n6), .Qout(q6));
  DivStep8 divstep8_8 (.R({n6[6:0], A[0]}), .B(B), .Qin(q6), .N(R), .Qout(Q));

  // Other names for the same wires on the sheet: n0_0 = n0[0]; rin1[7:0] = {n0[6:0], A[6]}; n0_1 = n0[1];
  //   n0_2 = n0[2]; n0_3 = n0[3]; n0_4 = n0[4]; n0_5 = n0[5]; n0_6 = n0[6]; n1_0 = n1[0]; rin2[7:0] = {n1[6:0], A[5]};
  //   n1_1 = n1[1]; n1_2 = n1[2]; n1_3 = n1[3]; n1_4 = n1[4]; n1_5 = n1[5]; n1_6 = n1[6]; n2_0 = n2[0];
  //   rin3[7:0] = {n2[6:0], A[4]}; n2_1 = n2[1]; n2_2 = n2[2]; n2_3 = n2[3]; n2_4 = n2[4]; n2_5 = n2[5]; n2_6 = n2[6];
  //   n3_0 = n3[0]; rin4[7:0] = {n3[6:0], A[3]}; n3_1 = n3[1]; n3_2 = n3[2]; n3_3 = n3[3]; n3_4 = n3[4]; n3_5 = n3[5];
  //   n3_6 = n3[6]; n4_0 = n4[0]; rin5[7:0] = {n4[6:0], A[2]}; n4_1 = n4[1]; n4_2 = n4[2]; n4_3 = n4[3]; n4_4 = n4[4];
  //   n4_5 = n4[5]; n4_6 = n4[6]; n5_0 = n5[0]; rin6[7:0] = {n5[6:0], A[1]}; n5_1 = n5[1]; n5_2 = n5[2]; n5_3 = n5[3];
  //   n5_4 = n5[4]; n5_5 = n5[5]; n5_6 = n5[6]; n6_0 = n6[0]; rin7[7:0] = {n6[6:0], A[0]}; n6_1 = n6[1]; n6_2 = n6[2];
  //   n6_3 = n6[3]; n6_4 = n6[4]; n6_5 = n6[5]; n6_6 = n6[6]; rin0[0] = A[7]
endmodule

module MUL8bit (
  input  [7:0] A,
  input  [7:0] B,
  output [7:0] Lo,
  output [7:0] Hi,
  output Ovf
);

  wire c1, c2, c3, c4, c5, c6, s0_1, s0_2, s0_3, s0_4, s0_5, s0_6, s0_7, s1_1, s1_2, s1_3, s1_4, s1_5, s1_6,
       s1_7, s2_1, s2_2, s2_3, s2_4, s2_5, s2_6, s2_7, s3_1, s3_2, s3_3, s3_4, s3_5, s3_6, s3_7, s4_1, s4_2,
       s4_3, s4_4, s4_5, s4_6, s4_7, s5_1, s5_2, s5_3, s5_4, s5_5, s5_6, s5_7, s6_1, s6_2, s6_3, s6_4, s6_5,
       s6_6, s6_7;
  wire [7:0] pp1, pp2, pp3, pp4, pp5, pp6, pp7;

  and and_1 (Lo[0], A[0], B[0]);
  and and_2 (s0_1, A[1], B[0]);
  and and_3 (s0_2, A[2], B[0]);
  and and_4 (s0_3, A[3], B[0]);
  and and_5 (s0_4, A[4], B[0]);
  and and_6 (s0_5, A[5], B[0]);
  and and_7 (s0_6, A[6], B[0]);
  and and_8 (s0_7, A[7], B[0]);
  and and_9 (pp1[0], A[0], B[1]);
  and and_10 (pp1[1], A[1], B[1]);
  and and_11 (pp1[2], A[2], B[1]);
  and and_12 (pp1[3], A[3], B[1]);
  and and_13 (pp1[4], A[4], B[1]);
  and and_14 (pp1[5], A[5], B[1]);
  and and_15 (pp1[6], A[6], B[1]);
  and and_16 (pp1[7], A[7], B[1]);
  and and_17 (pp2[0], A[0], B[2]);
  and and_18 (pp2[1], A[1], B[2]);
  and and_19 (pp2[2], A[2], B[2]);
  and and_20 (pp2[3], A[3], B[2]);
  and and_21 (pp2[4], A[4], B[2]);
  and and_22 (pp2[5], A[5], B[2]);
  and and_23 (pp2[6], A[6], B[2]);
  and and_24 (pp2[7], A[7], B[2]);
  and and_25 (pp3[0], A[0], B[3]);
  and and_26 (pp3[1], A[1], B[3]);
  and and_27 (pp3[2], A[2], B[3]);
  and and_28 (pp3[3], A[3], B[3]);
  and and_29 (pp3[4], A[4], B[3]);
  and and_30 (pp3[5], A[5], B[3]);
  and and_31 (pp3[6], A[6], B[3]);
  and and_32 (pp3[7], A[7], B[3]);
  and and_33 (pp4[0], A[0], B[4]);
  and and_34 (pp4[1], A[1], B[4]);
  and and_35 (pp4[2], A[2], B[4]);
  and and_36 (pp4[3], A[3], B[4]);
  and and_37 (pp4[4], A[4], B[4]);
  and and_38 (pp4[5], A[5], B[4]);
  and and_39 (pp4[6], A[6], B[4]);
  and and_40 (pp4[7], A[7], B[4]);
  and and_41 (pp5[0], A[0], B[5]);
  and and_42 (pp5[1], A[1], B[5]);
  and and_43 (pp5[2], A[2], B[5]);
  and and_44 (pp5[3], A[3], B[5]);
  and and_45 (pp5[4], A[4], B[5]);
  and and_46 (pp5[5], A[5], B[5]);
  and and_47 (pp5[6], A[6], B[5]);
  and and_48 (pp5[7], A[7], B[5]);
  and and_49 (pp6[0], A[0], B[6]);
  and and_50 (pp6[1], A[1], B[6]);
  and and_51 (pp6[2], A[2], B[6]);
  and and_52 (pp6[3], A[3], B[6]);
  and and_53 (pp6[4], A[4], B[6]);
  and and_54 (pp6[5], A[5], B[6]);
  and and_55 (pp6[6], A[6], B[6]);
  and and_56 (pp6[7], A[7], B[6]);
  and and_57 (pp7[0], A[0], B[7]);
  and and_58 (pp7[1], A[1], B[7]);
  and and_59 (pp7[2], A[2], B[7]);
  and and_60 (pp7[3], A[3], B[7]);
  and and_61 (pp7[4], A[4], B[7]);
  and and_62 (pp7[5], A[5], B[7]);
  and and_63 (pp7[6], A[6], B[7]);
  and and_64 (pp7[7], A[7], B[7]);
  Adder8bit adder8bit_1 (
    .A({1'b0, s0_7, s0_6, s0_5, s0_4, s0_3, s0_2, s0_1}), .B(pp1), .Cin(1'b0),
    .S({s1_7, s1_6, s1_5, s1_4, s1_3, s1_2, s1_1, Lo[1]}), .Cout(c1));  // open: V
  Adder8bit adder8bit_2 (
    .A({c1, s1_7, s1_6, s1_5, s1_4, s1_3, s1_2, s1_1}), .B(pp2), .Cin(1'b0),
    .S({s2_7, s2_6, s2_5, s2_4, s2_3, s2_2, s2_1, Lo[2]}), .Cout(c2));  // open: V
  Adder8bit adder8bit_3 (
    .A({c2, s2_7, s2_6, s2_5, s2_4, s2_3, s2_2, s2_1}), .B(pp3), .Cin(1'b0),
    .S({s3_7, s3_6, s3_5, s3_4, s3_3, s3_2, s3_1, Lo[3]}), .Cout(c3));  // open: V
  Adder8bit adder8bit_4 (
    .A({c3, s3_7, s3_6, s3_5, s3_4, s3_3, s3_2, s3_1}), .B(pp4), .Cin(1'b0),
    .S({s4_7, s4_6, s4_5, s4_4, s4_3, s4_2, s4_1, Lo[4]}), .Cout(c4));  // open: V
  Adder8bit adder8bit_5 (
    .A({c4, s4_7, s4_6, s4_5, s4_4, s4_3, s4_2, s4_1}), .B(pp5), .Cin(1'b0),
    .S({s5_7, s5_6, s5_5, s5_4, s5_3, s5_2, s5_1, Lo[5]}), .Cout(c5));  // open: V
  Adder8bit adder8bit_6 (
    .A({c5, s5_7, s5_6, s5_5, s5_4, s5_3, s5_2, s5_1}), .B(pp6), .Cin(1'b0),
    .S({s6_7, s6_6, s6_5, s6_4, s6_3, s6_2, s6_1, Lo[6]}), .Cout(c6));  // open: V
  Adder8bit adder8bit_7 (
    .A({c6, s6_7, s6_6, s6_5, s6_4, s6_3, s6_2, s6_1}), .B(pp7), .Cin(1'b0), .S({Hi[6:0], Lo[7]}),
    .Cout(Hi[7]));  // open: V
  or or_1 (Ovf, Hi[0], Hi[1], Hi[2], Hi[3], Hi[4], Hi[5], Hi[6], Hi[7]);

  // Other names for the same wires on the sheet: s7_1 = Hi[0]; sum7[7:0] = {Hi[6:0], Lo[7]}; s7_2 = Hi[1];
  //   s7_3 = Hi[2]; s7_4 = Hi[3]; s7_5 = Hi[4]; s7_6 = Hi[5]; s7_7 = Hi[6]; c7 = Hi[7]; s0_0 = Lo[0]; s1_0 = Lo[1];
  //   sum1[7:0] = {s1_7, s1_6, s1_5, s1_4, s1_3, s1_2, s1_1, Lo[1]}; s2_0 = Lo[2];
  //   sum2[7:0] = {s2_7, s2_6, s2_5, s2_4, s2_3, s2_2, s2_1, Lo[2]}; s3_0 = Lo[3];
  //   sum3[7:0] = {s3_7, s3_6, s3_5, s3_4, s3_3, s3_2, s3_1, Lo[3]}; s4_0 = Lo[4];
  //   sum4[7:0] = {s4_7, s4_6, s4_5, s4_4, s4_3, s4_2, s4_1, Lo[4]}; s5_0 = Lo[5];
  //   sum5[7:0] = {s5_7, s5_6, s5_5, s5_4, s5_3, s5_2, s5_1, Lo[5]}; s6_0 = Lo[6];
  //   sum6[7:0] = {s6_7, s6_6, s6_5, s6_4, s6_3, s6_2, s6_1, Lo[6]}; s7_0 = Lo[7]; pp1_0 = pp1[0]; pp1_1 = pp1[1];
  //   pp1_2 = pp1[2]; pp1_3 = pp1[3]; pp1_4 = pp1[4]; pp1_5 = pp1[5]; pp1_6 = pp1[6]; pp1_7 = pp1[7]; pp2_0 = pp2[0];
  //   pp2_1 = pp2[1]; pp2_2 = pp2[2]; pp2_3 = pp2[3]; pp2_4 = pp2[4]; pp2_5 = pp2[5]; pp2_6 = pp2[6]; pp2_7 = pp2[7];
  //   pp3_0 = pp3[0]; pp3_1 = pp3[1]; pp3_2 = pp3[2]; pp3_3 = pp3[3]; pp3_4 = pp3[4]; pp3_5 = pp3[5]; pp3_6 = pp3[6];
  //   pp3_7 = pp3[7]; pp4_0 = pp4[0]; pp4_1 = pp4[1]; pp4_2 = pp4[2]; pp4_3 = pp4[3]; pp4_4 = pp4[4]; pp4_5 = pp4[5];
  //   pp4_6 = pp4[6]; pp4_7 = pp4[7]; pp5_0 = pp5[0]; pp5_1 = pp5[1]; pp5_2 = pp5[2]; pp5_3 = pp5[3]; pp5_4 = pp5[4];
  //   pp5_5 = pp5[5]; pp5_6 = pp5[6]; pp5_7 = pp5[7]; pp6_0 = pp6[0]; pp6_1 = pp6[1]; pp6_2 = pp6[2]; pp6_3 = pp6[3];
  //   pp6_4 = pp6[4]; pp6_5 = pp6[5]; pp6_6 = pp6[6]; pp6_7 = pp6[7]; pp7_0 = pp7[0]; pp7_1 = pp7[1]; pp7_2 = pp7[2];
  //   pp7_3 = pp7[3]; pp7_4 = pp7[4]; pp7_5 = pp7[5]; pp7_6 = pp7[6]; pp7_7 = pp7[7];
  //   x2[7:0] = {c1, s1_7, s1_6, s1_5, s1_4, s1_3, s1_2, s1_1};
  //   x3[7:0] = {c2, s2_7, s2_6, s2_5, s2_4, s2_3, s2_2, s2_1};
  //   x4[7:0] = {c3, s3_7, s3_6, s3_5, s3_4, s3_3, s3_2, s3_1};
  //   x5[7:0] = {c4, s4_7, s4_6, s4_5, s4_4, s4_3, s4_2, s4_1};
  //   x6[7:0] = {c5, s5_7, s5_6, s5_5, s5_4, s5_3, s5_2, s5_1};
  //   x7[7:0] = {c6, s6_7, s6_6, s6_5, s6_4, s6_3, s6_2, s6_1}; x1[6:0] = {s0_7, s0_6, s0_5, s0_4, s0_3, s0_2, s0_1}
endmodule

module ShiftLeft8 (
  input  [7:0] A,
  input  [2:0] Amt,
  output [7:0] Y,
  output Cout
);

  wire cm0_0, cm0_1, cm0_2, cm0_3, cm1_0, cm1_1, st0_0, st0_1, st0_2, st0_3, st0_4, st0_5, st0_6, st0_7,
       st1_0, st1_1, st1_2, st1_3, st1_4, st1_5, st1_6, st1_7;

  Select1bit select1bit_1 (.Sel(Amt[0]), .X(A[0]), .Y(1'b0), .SelOut(st0_0));
  Select1bit select1bit_2 (.Sel(Amt[0]), .X(A[1]), .Y(A[0]), .SelOut(st0_1));
  Select1bit select1bit_3 (.Sel(Amt[0]), .X(A[2]), .Y(A[1]), .SelOut(st0_2));
  Select1bit select1bit_4 (.Sel(Amt[0]), .X(A[3]), .Y(A[2]), .SelOut(st0_3));
  Select1bit select1bit_5 (.Sel(Amt[0]), .X(A[4]), .Y(A[3]), .SelOut(st0_4));
  Select1bit select1bit_6 (.Sel(Amt[0]), .X(A[5]), .Y(A[4]), .SelOut(st0_5));
  Select1bit select1bit_7 (.Sel(Amt[0]), .X(A[6]), .Y(A[5]), .SelOut(st0_6));
  Select1bit select1bit_8 (.Sel(Amt[0]), .X(A[7]), .Y(A[6]), .SelOut(st0_7));
  Select1bit select1bit_9 (.Sel(Amt[1]), .X(st0_0), .Y(1'b0), .SelOut(st1_0));
  Select1bit select1bit_10 (.Sel(Amt[1]), .X(st0_1), .Y(1'b0), .SelOut(st1_1));
  Select1bit select1bit_11 (.Sel(Amt[1]), .X(st0_2), .Y(st0_0), .SelOut(st1_2));
  Select1bit select1bit_12 (.Sel(Amt[1]), .X(st0_3), .Y(st0_1), .SelOut(st1_3));
  Select1bit select1bit_13 (.Sel(Amt[1]), .X(st0_4), .Y(st0_2), .SelOut(st1_4));
  Select1bit select1bit_14 (.Sel(Amt[1]), .X(st0_5), .Y(st0_3), .SelOut(st1_5));
  Select1bit select1bit_15 (.Sel(Amt[1]), .X(st0_6), .Y(st0_4), .SelOut(st1_6));
  Select1bit select1bit_16 (.Sel(Amt[1]), .X(st0_7), .Y(st0_5), .SelOut(st1_7));
  Select1bit select1bit_17 (.Sel(Amt[2]), .X(st1_0), .Y(1'b0), .SelOut(Y[0]));
  Select1bit select1bit_18 (.Sel(Amt[2]), .X(st1_1), .Y(1'b0), .SelOut(Y[1]));
  Select1bit select1bit_19 (.Sel(Amt[2]), .X(st1_2), .Y(1'b0), .SelOut(Y[2]));
  Select1bit select1bit_20 (.Sel(Amt[2]), .X(st1_3), .Y(1'b0), .SelOut(Y[3]));
  Select1bit select1bit_21 (.Sel(Amt[2]), .X(st1_4), .Y(st1_0), .SelOut(Y[4]));
  Select1bit select1bit_22 (.Sel(Amt[2]), .X(st1_5), .Y(st1_1), .SelOut(Y[5]));
  Select1bit select1bit_23 (.Sel(Amt[2]), .X(st1_6), .Y(st1_2), .SelOut(Y[6]));
  Select1bit select1bit_24 (.Sel(Amt[2]), .X(st1_7), .Y(st1_3), .SelOut(Y[7]));
  Select1bit select1bit_25 (.Sel(Amt[0]), .X(1'b0), .Y(A[7]), .SelOut(cm0_0));
  Select1bit select1bit_26 (.Sel(Amt[0]), .X(A[6]), .Y(A[5]), .SelOut(cm0_1));
  Select1bit select1bit_27 (.Sel(Amt[0]), .X(A[4]), .Y(A[3]), .SelOut(cm0_2));
  Select1bit select1bit_28 (.Sel(Amt[0]), .X(A[2]), .Y(A[1]), .SelOut(cm0_3));
  Select1bit select1bit_29 (.Sel(Amt[1]), .X(cm0_0), .Y(cm0_1), .SelOut(cm1_0));
  Select1bit select1bit_30 (.Sel(Amt[1]), .X(cm0_2), .Y(cm0_3), .SelOut(cm1_1));
  Select1bit select1bit_31 (.Sel(Amt[2]), .X(cm1_0), .Y(cm1_1), .SelOut(Cout));
endmodule

module ShiftRight8 (
  input  [7:0] A,
  input  [2:0] Amt,
  input  Arith,
  output [7:0] Y,
  output Cout
);

  wire cm0_0, cm0_1, cm0_2, cm0_3, cm1_0, cm1_1, fill, st0_0, st0_1, st0_2, st0_3, st0_4, st0_5, st0_6,
       st0_7, st1_0, st1_1, st1_2, st1_3, st1_4, st1_5, st1_6, st1_7;

  and and_1 (fill, A[7], Arith);
  Select1bit select1bit_1 (.Sel(Amt[0]), .X(A[0]), .Y(A[1]), .SelOut(st0_0));
  Select1bit select1bit_2 (.Sel(Amt[0]), .X(A[1]), .Y(A[2]), .SelOut(st0_1));
  Select1bit select1bit_3 (.Sel(Amt[0]), .X(A[2]), .Y(A[3]), .SelOut(st0_2));
  Select1bit select1bit_4 (.Sel(Amt[0]), .X(A[3]), .Y(A[4]), .SelOut(st0_3));
  Select1bit select1bit_5 (.Sel(Amt[0]), .X(A[4]), .Y(A[5]), .SelOut(st0_4));
  Select1bit select1bit_6 (.Sel(Amt[0]), .X(A[5]), .Y(A[6]), .SelOut(st0_5));
  Select1bit select1bit_7 (.Sel(Amt[0]), .X(A[6]), .Y(A[7]), .SelOut(st0_6));
  Select1bit select1bit_8 (.Sel(Amt[0]), .X(A[7]), .Y(fill), .SelOut(st0_7));
  Select1bit select1bit_9 (.Sel(Amt[1]), .X(st0_0), .Y(st0_2), .SelOut(st1_0));
  Select1bit select1bit_10 (.Sel(Amt[1]), .X(st0_1), .Y(st0_3), .SelOut(st1_1));
  Select1bit select1bit_11 (.Sel(Amt[1]), .X(st0_2), .Y(st0_4), .SelOut(st1_2));
  Select1bit select1bit_12 (.Sel(Amt[1]), .X(st0_3), .Y(st0_5), .SelOut(st1_3));
  Select1bit select1bit_13 (.Sel(Amt[1]), .X(st0_4), .Y(st0_6), .SelOut(st1_4));
  Select1bit select1bit_14 (.Sel(Amt[1]), .X(st0_5), .Y(st0_7), .SelOut(st1_5));
  Select1bit select1bit_15 (.Sel(Amt[1]), .X(st0_6), .Y(fill), .SelOut(st1_6));
  Select1bit select1bit_16 (.Sel(Amt[1]), .X(st0_7), .Y(fill), .SelOut(st1_7));
  Select1bit select1bit_17 (.Sel(Amt[2]), .X(st1_0), .Y(st1_4), .SelOut(Y[0]));
  Select1bit select1bit_18 (.Sel(Amt[2]), .X(st1_1), .Y(st1_5), .SelOut(Y[1]));
  Select1bit select1bit_19 (.Sel(Amt[2]), .X(st1_2), .Y(st1_6), .SelOut(Y[2]));
  Select1bit select1bit_20 (.Sel(Amt[2]), .X(st1_3), .Y(st1_7), .SelOut(Y[3]));
  Select1bit select1bit_21 (.Sel(Amt[2]), .X(st1_4), .Y(fill), .SelOut(Y[4]));
  Select1bit select1bit_22 (.Sel(Amt[2]), .X(st1_5), .Y(fill), .SelOut(Y[5]));
  Select1bit select1bit_23 (.Sel(Amt[2]), .X(st1_6), .Y(fill), .SelOut(Y[6]));
  Select1bit select1bit_24 (.Sel(Amt[2]), .X(st1_7), .Y(fill), .SelOut(Y[7]));
  Select1bit select1bit_25 (.Sel(Amt[0]), .X(1'b0), .Y(A[0]), .SelOut(cm0_0));
  Select1bit select1bit_26 (.Sel(Amt[0]), .X(A[1]), .Y(A[2]), .SelOut(cm0_1));
  Select1bit select1bit_27 (.Sel(Amt[0]), .X(A[3]), .Y(A[4]), .SelOut(cm0_2));
  Select1bit select1bit_28 (.Sel(Amt[0]), .X(A[5]), .Y(A[6]), .SelOut(cm0_3));
  Select1bit select1bit_29 (.Sel(Amt[1]), .X(cm0_0), .Y(cm0_1), .SelOut(cm1_0));
  Select1bit select1bit_30 (.Sel(Amt[1]), .X(cm0_2), .Y(cm0_3), .SelOut(cm1_1));
  Select1bit select1bit_31 (.Sel(Amt[2]), .X(cm1_0), .Y(cm1_1), .SelOut(Cout));
endmodule

module RotateLeft8 (
  input  [7:0] A,
  input  [2:0] Amt,
  output [7:0] Y
);

  wire st0_0, st0_1, st0_2, st0_3, st0_4, st0_5, st0_6, st0_7, st1_0, st1_1, st1_2, st1_3, st1_4, st1_5,
       st1_6, st1_7;

  Select1bit select1bit_1 (.Sel(Amt[0]), .X(A[0]), .Y(A[7]), .SelOut(st0_0));
  Select1bit select1bit_2 (.Sel(Amt[0]), .X(A[1]), .Y(A[0]), .SelOut(st0_1));
  Select1bit select1bit_3 (.Sel(Amt[0]), .X(A[2]), .Y(A[1]), .SelOut(st0_2));
  Select1bit select1bit_4 (.Sel(Amt[0]), .X(A[3]), .Y(A[2]), .SelOut(st0_3));
  Select1bit select1bit_5 (.Sel(Amt[0]), .X(A[4]), .Y(A[3]), .SelOut(st0_4));
  Select1bit select1bit_6 (.Sel(Amt[0]), .X(A[5]), .Y(A[4]), .SelOut(st0_5));
  Select1bit select1bit_7 (.Sel(Amt[0]), .X(A[6]), .Y(A[5]), .SelOut(st0_6));
  Select1bit select1bit_8 (.Sel(Amt[0]), .X(A[7]), .Y(A[6]), .SelOut(st0_7));
  Select1bit select1bit_9 (.Sel(Amt[1]), .X(st0_0), .Y(st0_6), .SelOut(st1_0));
  Select1bit select1bit_10 (.Sel(Amt[1]), .X(st0_1), .Y(st0_7), .SelOut(st1_1));
  Select1bit select1bit_11 (.Sel(Amt[1]), .X(st0_2), .Y(st0_0), .SelOut(st1_2));
  Select1bit select1bit_12 (.Sel(Amt[1]), .X(st0_3), .Y(st0_1), .SelOut(st1_3));
  Select1bit select1bit_13 (.Sel(Amt[1]), .X(st0_4), .Y(st0_2), .SelOut(st1_4));
  Select1bit select1bit_14 (.Sel(Amt[1]), .X(st0_5), .Y(st0_3), .SelOut(st1_5));
  Select1bit select1bit_15 (.Sel(Amt[1]), .X(st0_6), .Y(st0_4), .SelOut(st1_6));
  Select1bit select1bit_16 (.Sel(Amt[1]), .X(st0_7), .Y(st0_5), .SelOut(st1_7));
  Select1bit select1bit_17 (.Sel(Amt[2]), .X(st1_0), .Y(st1_4), .SelOut(Y[0]));
  Select1bit select1bit_18 (.Sel(Amt[2]), .X(st1_1), .Y(st1_5), .SelOut(Y[1]));
  Select1bit select1bit_19 (.Sel(Amt[2]), .X(st1_2), .Y(st1_6), .SelOut(Y[2]));
  Select1bit select1bit_20 (.Sel(Amt[2]), .X(st1_3), .Y(st1_7), .SelOut(Y[3]));
  Select1bit select1bit_21 (.Sel(Amt[2]), .X(st1_4), .Y(st1_0), .SelOut(Y[4]));
  Select1bit select1bit_22 (.Sel(Amt[2]), .X(st1_5), .Y(st1_1), .SelOut(Y[5]));
  Select1bit select1bit_23 (.Sel(Amt[2]), .X(st1_6), .Y(st1_2), .SelOut(Y[6]));
  Select1bit select1bit_24 (.Sel(Amt[2]), .X(st1_7), .Y(st1_3), .SelOut(Y[7]));
endmodule

module RotateRight8 (
  input  [7:0] A,
  input  [2:0] Amt,
  output [7:0] Y
);

  wire st0_0, st0_1, st0_2, st0_3, st0_4, st0_5, st0_6, st0_7, st1_0, st1_1, st1_2, st1_3, st1_4, st1_5,
       st1_6, st1_7;

  Select1bit select1bit_1 (.Sel(Amt[0]), .X(A[0]), .Y(A[1]), .SelOut(st0_0));
  Select1bit select1bit_2 (.Sel(Amt[0]), .X(A[1]), .Y(A[2]), .SelOut(st0_1));
  Select1bit select1bit_3 (.Sel(Amt[0]), .X(A[2]), .Y(A[3]), .SelOut(st0_2));
  Select1bit select1bit_4 (.Sel(Amt[0]), .X(A[3]), .Y(A[4]), .SelOut(st0_3));
  Select1bit select1bit_5 (.Sel(Amt[0]), .X(A[4]), .Y(A[5]), .SelOut(st0_4));
  Select1bit select1bit_6 (.Sel(Amt[0]), .X(A[5]), .Y(A[6]), .SelOut(st0_5));
  Select1bit select1bit_7 (.Sel(Amt[0]), .X(A[6]), .Y(A[7]), .SelOut(st0_6));
  Select1bit select1bit_8 (.Sel(Amt[0]), .X(A[7]), .Y(A[0]), .SelOut(st0_7));
  Select1bit select1bit_9 (.Sel(Amt[1]), .X(st0_0), .Y(st0_2), .SelOut(st1_0));
  Select1bit select1bit_10 (.Sel(Amt[1]), .X(st0_1), .Y(st0_3), .SelOut(st1_1));
  Select1bit select1bit_11 (.Sel(Amt[1]), .X(st0_2), .Y(st0_4), .SelOut(st1_2));
  Select1bit select1bit_12 (.Sel(Amt[1]), .X(st0_3), .Y(st0_5), .SelOut(st1_3));
  Select1bit select1bit_13 (.Sel(Amt[1]), .X(st0_4), .Y(st0_6), .SelOut(st1_4));
  Select1bit select1bit_14 (.Sel(Amt[1]), .X(st0_5), .Y(st0_7), .SelOut(st1_5));
  Select1bit select1bit_15 (.Sel(Amt[1]), .X(st0_6), .Y(st0_0), .SelOut(st1_6));
  Select1bit select1bit_16 (.Sel(Amt[1]), .X(st0_7), .Y(st0_1), .SelOut(st1_7));
  Select1bit select1bit_17 (.Sel(Amt[2]), .X(st1_0), .Y(st1_4), .SelOut(Y[0]));
  Select1bit select1bit_18 (.Sel(Amt[2]), .X(st1_1), .Y(st1_5), .SelOut(Y[1]));
  Select1bit select1bit_19 (.Sel(Amt[2]), .X(st1_2), .Y(st1_6), .SelOut(Y[2]));
  Select1bit select1bit_20 (.Sel(Amt[2]), .X(st1_3), .Y(st1_7), .SelOut(Y[3]));
  Select1bit select1bit_21 (.Sel(Amt[2]), .X(st1_4), .Y(st1_0), .SelOut(Y[4]));
  Select1bit select1bit_22 (.Sel(Amt[2]), .X(st1_5), .Y(st1_1), .SelOut(Y[5]));
  Select1bit select1bit_23 (.Sel(Amt[2]), .X(st1_6), .Y(st1_2), .SelOut(Y[6]));
  Select1bit select1bit_24 (.Sel(Amt[2]), .X(st1_7), .Y(st1_3), .SelOut(Y[7]));
endmodule

module ALUCore8 (
  input  [7:0] A,
  input  [7:0] B,
  input  [3:0] Op,
  output [7:0] R,
  output Z,
  output C,
  output S,
  output V
);

  wire c0, c1, c2, c3, c11, c12, c13;
  wire [1:1] cv0, cv1, cv2, cv3, cv4, cv10;
  wire [7:0] r0, r1, r2, r3, r4, r5, r6, r7, r8, r9, r10, r11, r12, r13, r14, r15;

  Adder8bit adder8bit_1 (.A(A), .B(B), .Cin(1'b0), .S(r0), .Cout(c0), .V(cv0[1]));
  Subtractor8bit subtractor8bit_1 (.A(A), .B(B), .S(r1), .Cout(c1), .V(cv1[1]));
  INC8bit inc8bit_1 (.A(A), .S(r2), .Cout(c2), .V(cv2[1]));
  DEC8bit dec8bit_1 (.A(A), .S(r3), .Cout(c3), .V(cv3[1]));
  LogicUnit8 logicunit8_1 (.A(A), .B(B), .And(r5), .Or(r6), .Xor(r7), .NotA(r8));
  DIV8bit div8bit_1 (.A(A), .B(B), .Q(r4), .R(r9), .DZ(cv4[1]));
  MUL8bit mul8bit_1 (.A(A), .B(B), .Lo(r10), .Ovf(cv10[1]));  // open: Hi
  ShiftLeft8 shiftleft8_1 (.A(A), .Amt(B[2:0]), .Y(r11), .Cout(c11));
  ShiftRight8 shiftright8_1 (.A(A), .Amt(B[2:0]), .Arith(1'b0), .Y(r12), .Cout(c12));
  ShiftRight8 shiftright8_2 (.A(A), .Amt(B[2:0]), .Arith(1'b1), .Y(r13), .Cout(c13));
  RotateLeft8 rotateleft8_1 (.A(A), .Amt(B[2:0]), .Y(r14));
  RotateRight8 rotateright8_1 (.A(A), .Amt(B[2:0]), .Y(r15));
  OpMux16x8 opmux16x8_1 (
    .Sel(Op), .In0(r0), .In1(r1), .In2(r2), .In3(r3), .In4(r4), .In5(r5), .In6(r6), .In7(r7), .In8(r8),
    .In9(r9), .In10(r10), .In11(r11), .In12(r12), .In13(r13), .In14(r14), .In15(r15), .Out(R));
  OpMux16x2 opmux16x2_1 (
    .Sel(Op), .In0({cv0[1], c0}), .In1({cv1[1], c1}), .In2({cv2[1], c2}), .In3({cv3[1], c3}),
    .In4({cv4[1], 1'b0}), .In5(2'b00), .In6(2'b00), .In7(2'b00), .In8(2'b00), .In9({cv4[1], 1'b0}),
    .In10({2{cv10[1]}}), .In11({1'b0, c11}), .In12({1'b0, c12}), .In13({1'b0, c13}), .In14(2'b00),
    .In15(2'b00), .Out({V, C}));
  ZeroDetect8 zerodetect8_1 (.In(R), .Z(Z));

  assign S = R[7];

  // Other names for the same wires on the sheet: Amt[2:0] = B[2:0]; cv0[0] = c0; v0 = cv0[1]; cv1[0] = c1;
  //   v1 = cv1[1]; cv2[0] = c2; v2 = cv2[1]; cv3[0] = c3; v3 = cv3[1]; cv9[1] = cv4[1]; dz = cv4[1];
  //   cv10[0] = cv10[1]; ovf = cv10[1]; cv11[0] = c11; cv12[0] = c12; cv13[0] = c13; cvout[1:0] = {V, C}
endmodule

module HexDecoder7 (
  input  [3:0] In,
  output a,
  output b,
  output c,
  output d,
  output e,
  output f,
  output g
);

  wire d0, d1, d2, d3, d4, d5, d6, d7, d8, d9, d10, d11, d12, d13, d14, d15, ni0, ni1, ni2, ni3;

  not not_1 (ni0, In[0]);
  not not_2 (ni1, In[1]);
  not not_3 (ni2, In[2]);
  not not_4 (ni3, In[3]);
  and and_1 (d0, ni0, ni1, ni2, ni3);
  and and_2 (d1, In[0], ni1, ni2, ni3);
  and and_3 (d2, ni0, In[1], ni2, ni3);
  and and_4 (d3, In[0], In[1], ni2, ni3);
  and and_5 (d4, ni0, ni1, In[2], ni3);
  and and_6 (d5, In[0], ni1, In[2], ni3);
  and and_7 (d6, ni0, In[1], In[2], ni3);
  and and_8 (d7, In[0], In[1], In[2], ni3);
  and and_9 (d8, ni0, ni1, ni2, In[3]);
  and and_10 (d9, In[0], ni1, ni2, In[3]);
  and and_11 (d10, ni0, In[1], ni2, In[3]);
  and and_12 (d11, In[0], In[1], ni2, In[3]);
  and and_13 (d12, ni0, ni1, In[2], In[3]);
  and and_14 (d13, In[0], ni1, In[2], In[3]);
  and and_15 (d14, ni0, In[1], In[2], In[3]);
  and and_16 (d15, In[0], In[1], In[2], In[3]);
  or or_1 (a, d0, d2, d3, d5, d6, d7, d8, d9, d10, d12, d14, d15);
  or or_2 (b, d0, d1, d2, d3, d4, d7, d8, d9, d10, d13);
  or or_3 (c, d0, d1, d3, d4, d5, d6, d7, d8, d9, d10, d11, d13);
  or or_4 (d, d0, d2, d3, d5, d6, d8, d9, d11, d12, d13, d14);
  or or_5 (e, d0, d2, d6, d8, d10, d11, d12, d13, d14, d15);
  or or_6 (f, d0, d4, d5, d6, d8, d9, d10, d11, d12, d14, d15);
  or or_7 (g, d2, d3, d4, d5, d6, d8, d9, d10, d11, d13, d14, d15);

  // Other names for the same wires on the sheet: i0 = In[0]; i1 = In[1]; i2 = In[2]; i3 = In[3]
endmodule

module Add3 (
  input  [3:0] In,
  output [3:0] Out
);

  wire c1, c2, c3, ge5, x10, x210;

  or or_1 (x10, In[1], In[0]);
  and and_1 (x210, In[2], x10);
  or or_2 (ge5, In[3], x210);
  HalfAdder halfadder_1 (.A(In[0]), .B(ge5), .Sum(Out[0]), .Carry(c1));
  FullAdder fulladder_1 (.A(In[1]), .B(ge5), .Cin(c1), .Sum(Out[1]), .Cout(c2));
  HalfAdder halfadder_2 (.A(In[2]), .B(c2), .Sum(Out[2]), .Carry(c3));
  xor xor_1 (Out[3], In[3], c3);

  // Other names for the same wires on the sheet: x0 = In[0]; x1 = In[1]; x2 = In[2]; x3 = In[3]; y0 = Out[0];
  //   y1 = Out[1]; y2 = Out[2]; y3 = Out[3]
endmodule

module BinToBCD8 (
  input  [7:0] In,
  output [3:0] Hundreds,
  output [3:0] Tens,
  output [3:0] Ones
);

  wire [2:0] in6;
  wire [3:0] in7;
  wire [3:1] in2, in3, in4, in5;

  Add3 add3_1 (.In({1'b0, In[7:5]}), .Out({in6[2], in2}));
  Add3 add3_2 (.In({in2, In[4]}), .Out({in6[1], in3}));
  Add3 add3_3 (.In({in3, In[3]}), .Out({in6[0], in4}));
  Add3 add3_4 (.In({in4, In[2]}), .Out({in7[0], in5}));
  Add3 add3_5 (.In({in5, In[1]}), .Out({Tens[0], Ones[3:1]}));
  Add3 add3_6 (.In({1'b0, in6}), .Out({Hundreds[1], in7[3:1]}));
  Add3 add3_7 (.In(in7), .Out({Hundreds[0], Tens[3:1]}));

  assign Hundreds[3:2] = 2'b00;
  assign Ones[0] = In[0];

  // Other names for the same wires on the sheet: o7_3 = Hundreds[0]; out7[3:0] = {Hundreds[0], Tens[3:1]};
  //   o6_3 = Hundreds[1]; out6[3:0] = {Hundreds[1], in7[3:1]}; i5 = In[5]; in1[2:0] = In[7:5]; i6 = In[6]; i7 = In[7];
  //   i4 = In[4]; in2[0] = In[4]; i3 = In[3]; in3[0] = In[3]; i2 = In[2]; in4[0] = In[2]; i1 = In[1]; in5[0] = In[1];
  //   i0 = In[0]; o5_0 = Ones[1]; out5[3:0] = {Tens[0], Ones[3:1]}; o5_1 = Ones[2]; o5_2 = Ones[3]; o1_0 = in2[1];
  //   out1[3:0] = {in6[2], in2}; o1_1 = in2[2]; o1_2 = in2[3]; o1_3 = in6[2]; o2_0 = in3[1];
  //   out2[3:0] = {in6[1], in3}; o2_1 = in3[2]; o2_2 = in3[3]; o2_3 = in6[1]; o3_0 = in4[1];
  //   out3[3:0] = {in6[0], in4}; o3_1 = in4[2]; o3_2 = in4[3]; o3_3 = in6[0]; o4_0 = in5[1];
  //   out4[3:0] = {in7[0], in5}; o4_1 = in5[2]; o4_2 = in5[3]; o4_3 = in7[0]; o6_0 = in7[1]; o6_1 = in7[2];
  //   o6_2 = in7[3]; o5_3 = Tens[0]; o7_0 = Tens[1]; o7_1 = Tens[2]; o7_2 = Tens[3]
endmodule

module ControlUnit (
  input  CLK,
  input  Reset,
  input  Load,
  input  Execute,
  output LoadAB,
  output LoadOut,
  output S0,
  output S1
);

  wire adv0, adv1, d0, d1, go_disp, go_load, nreset, ns0, ns1;

  not not_1 (nreset, Reset);
  and and_1 (go_load, ns1, ns0, Load);
  and and_2 (go_disp, S1, ns0, Execute);
  xor xor_1 (adv1, S1, S0);
  or or_1 (adv0, go_load, go_disp);
  and and_3 (d0, adv0, nreset);
  and and_4 (d1, adv1, nreset);
  D_Flip_Flop d_ff_1 (.D(d0), .clk(CLK), .Q(S0), .Qn(ns0));  // open: preset, reset
  D_Flip_Flop d_ff_2 (.D(d1), .clk(CLK), .Q(S1), .Qn(ns1));  // open: preset, reset
  and and_5 (LoadAB, ns1, S0);
  and and_6 (LoadOut, S1, ns0);
endmodule

module main (
  input  [7:0] A,
  input  [7:0] B,
  input  [3:0] Op,
  input  Load,
  input  Execute,
  input  Reset,
  output [7:0] R,
  output Z,
  output C,
  output S,
  output V,
  output S0,
  output S1,
  output [11:0] Dec
);

  wire c_t, clk, dh_a, dh_a_on, dh_b, dh_b_on, dh_c, dh_c_on, dh_d, dh_d_on, dh_e, dh_e_on, dh_f, dh_f_on,
       dh_g, dh_g_on, do_a_on, do_b_on, do_c_on, do_d_on, do_e_on, do_f_on, do_g_on, dt_a, dt_a_on, dt_b,
       dt_b_on, dt_c, dt_c_on, dt_d, dt_d_on, dt_e, dt_e_on, dt_f, dt_f_on, dt_g, dt_g_on, hi_a, hi_b, hi_c,
       hi_d, hi_e, hi_f, hi_g, hon, lab, lo_a, lo_b, lo_c, lo_d, lo_e, lo_f, lo_g, lout, s_t, ton, v_t, z_t;
  wire [7:0] qa, qb, r_t;

  Clock u_CLK (.out(clk));
  ControlUnit controlunit_1 (
    .CLK(clk), .Reset(Reset), .Load(Load), .Execute(Execute), .LoadAB(lab), .LoadOut(lout), .S0(S0), .S1(S1));
  Register8bit RegisterA (.Load(lab), .D(A), .CLK(clk), .Q(qa));
  Register8bit RegisterB (.Load(lab), .D(B), .CLK(clk), .Q(qb));
  ALUCore8 alucore8_1 (.A(qa), .B(qb), .Op(Op), .R(r_t), .Z(z_t), .C(c_t), .S(s_t), .V(v_t));
  Register8bit OutputRegister (.Load(lout), .D(r_t), .CLK(clk), .Q(R));
  Register4bit FlagRegister (
    .Load(lout), .D0(z_t), .D1(c_t), .D2(s_t), .D3(v_t), .CLK(clk), .Q0(Z), .Q1(C), .Q2(S), .Q3(V));
  BinToBCD8 bintobcd8_1 (.In(R), .Hundreds(Dec[11:8]), .Tens(Dec[7:4]), .Ones(Dec[3:0]));
  or or_1 (hon, Dec[8], Dec[9], Dec[10], Dec[11]);
  or or_2 (ton, hon, Dec[4], Dec[5], Dec[6], Dec[7]);
  HexDecoder7 hexdecoder7_1 (.In(R[7:4]), .a(hi_a), .b(hi_b), .c(hi_c), .d(hi_d), .e(hi_e), .f(hi_f), .g(hi_g));
  HexDecoder7 hexdecoder7_2 (.In(R[3:0]), .a(lo_a), .b(lo_b), .c(lo_c), .d(lo_d), .e(lo_e), .f(lo_f), .g(lo_g));
  HexDecoder7 hexdecoder7_3 (.In(Dec[11:8]), .a(dh_a), .b(dh_b), .c(dh_c), .d(dh_d), .e(dh_e), .f(dh_f), .g(dh_g));
  HexDecoder7 hexdecoder7_4 (.In(Dec[7:4]), .a(dt_a), .b(dt_b), .c(dt_c), .d(dt_d), .e(dt_e), .f(dt_f), .g(dt_g));
  HexDecoder7 hexdecoder7_5 (
    .In(Dec[3:0]), .a(do_a_on), .b(do_b_on), .c(do_c_on), .d(do_d_on), .e(do_e_on), .f(do_f_on), .g(do_g_on));
  and and_1 (dh_a_on, dh_a, hon);
  and and_2 (dh_b_on, dh_b, hon);
  and and_3 (dh_c_on, dh_c, hon);
  and and_4 (dh_d_on, dh_d, hon);
  and and_5 (dh_e_on, dh_e, hon);
  and and_6 (dh_f_on, dh_f, hon);
  and and_7 (dh_g_on, dh_g, hon);
  and and_8 (dt_a_on, dt_a, ton);
  and and_9 (dt_b_on, dt_b, ton);
  and and_10 (dt_c_on, dt_c, ton);
  and and_11 (dt_d_on, dt_d, ton);
  and and_12 (dt_e_on, dt_e, ton);
  and and_13 (dt_f_on, dt_f, ton);
  and and_14 (dt_g_on, dt_g, ton);
  _7_Segment_Display u_7_segment_display_1 (
    .g(hi_g), .f(hi_f), .a(hi_a), .b(hi_b), .e(hi_e), .d(hi_d), .c(hi_c));  // open: dp
  _7_Segment_Display u_7_segment_display_2 (
    .g(lo_g), .f(lo_f), .a(lo_a), .b(lo_b), .e(lo_e), .d(lo_d), .c(lo_c));  // open: dp
  _7_Segment_Display u_7_segment_display_3 (
    .g(dh_g_on), .f(dh_f_on), .a(dh_a_on), .b(dh_b_on), .e(dh_e_on), .d(dh_d_on), .c(dh_c_on));  // open: dp
  _7_Segment_Display u_7_segment_display_4 (
    .g(dt_g_on), .f(dt_f_on), .a(dt_a_on), .b(dt_b_on), .e(dt_e_on), .d(dt_d_on), .c(dt_c_on));  // open: dp
  _7_Segment_Display u_7_segment_display_5 (
    .g(do_g_on), .f(do_f_on), .a(do_a_on), .b(do_b_on), .e(do_e_on), .d(do_d_on), .c(do_c_on));  // open: dp
  LED ZLed (.in(Z));
  LED CLed (.in(C));
  LED SLed (.in(S));
  LED VLed (.in(V));
  LED State0Led (.in(S0));
  LED State1Led (.in(S1));

  // Other names for the same wires on the sheet: do[3:0] = Dec[3:0]; do0 = Dec[0]; do1 = Dec[1]; do2 = Dec[2];
  //   do3 = Dec[3]; dt[3:0] = Dec[7:4]; dt0 = Dec[4]; dt1 = Dec[5]; dt2 = Dec[6]; dt3 = Dec[7]; dh[3:0] = Dec[11:8];
  //   dh0 = Dec[8]; dh1 = Dec[9]; dh2 = Dec[10]; dh3 = Dec[11]; rq4 = R[4]; rq_hi[3:0] = R[7:4]; rq5 = R[5];
  //   rq6 = R[6]; rq7 = R[7]; rq0 = R[0]; rq_lo[3:0] = R[3:0]; rq1 = R[1]; rq2 = R[2]; rq3 = R[3]
endmodule

module RegFile4x8 (
  input  [7:0] D,
  input  [1:0] WSel,
  input  WE,
  input  [1:0] RSelA,
  input  [1:0] RSelB,
  input  CLK,
  input  Reset,
  output [7:0] QA,
  output [7:0] QB,
  output [7:0] R0,
  output [7:0] R1,
  output [7:0] R2,
  output [7:0] R3
);

  wire ld0, ld1, ld2, ld3, nw0, nw1, we0, we1, we2, we3;
  wire [7:0] a01, a23, b01, b23, dd;

  not not_1 (nw0, WSel[0]);
  not not_2 (nw1, WSel[1]);
  Select8bit select8bit_1 (.Sel(Reset), .X(D), .Y({8{1'b0}}), .Out(dd));
  and and_1 (we0, WE, nw1, nw0);
  and and_2 (we1, WE, nw1, WSel[0]);
  and and_3 (we2, WE, WSel[1], nw0);
  and and_4 (we3, WE, WSel[1], WSel[0]);
  or or_1 (ld0, we0, Reset);
  or or_2 (ld1, we1, Reset);
  or or_3 (ld2, we2, Reset);
  or or_4 (ld3, we3, Reset);
  Register8bit u_R0 (.Load(ld0), .D(dd), .CLK(CLK), .Q(R0));
  Register8bit u_R1 (.Load(ld1), .D(dd), .CLK(CLK), .Q(R1));
  Register8bit u_R2 (.Load(ld2), .D(dd), .CLK(CLK), .Q(R2));
  Register8bit u_R3 (.Load(ld3), .D(dd), .CLK(CLK), .Q(R3));
  Select8bit select8bit_2 (.Sel(RSelA[0]), .X(R0), .Y(R1), .Out(a01));
  Select8bit select8bit_3 (.Sel(RSelA[0]), .X(R2), .Y(R3), .Out(a23));
  Select8bit select8bit_4 (.Sel(RSelA[1]), .X(a01), .Y(a23), .Out(QA));
  Select8bit select8bit_5 (.Sel(RSelB[0]), .X(R0), .Y(R1), .Out(b01));
  Select8bit select8bit_6 (.Sel(RSelB[0]), .X(R2), .Y(R3), .Out(b23));
  Select8bit select8bit_7 (.Sel(RSelB[1]), .X(b01), .Y(b23), .Out(QB));

  // Other names for the same wires on the sheet: as0 = RSelA[0]; as1 = RSelA[1]; bs0 = RSelB[0]; bs1 = RSelB[1];
  //   w0 = WSel[0]; w1 = WSel[1]
endmodule

module PC8 (
  input  [7:0] D,
  input  Jump,
  input  Hold,
  input  CLK,
  input  Reset,
  output [7:0] Q
);

  wire ld, nhold;
  wire [7:0] dd, inc, nx;

  INC8bit inc8bit_1 (.A(Q), .S(inc));  // open: Cout, V
  not not_1 (nhold, Hold);
  Select8bit select8bit_1 (.Sel(Jump), .X(inc), .Y(D), .Out(nx));
  or or_1 (ld, nhold, Reset);
  Select8bit select8bit_2 (.Sel(Reset), .X(nx), .Y({8{1'b0}}), .Out(dd));
  Register8bit register8bit_1 (.Load(ld), .D(dd), .CLK(CLK), .Q(Q));
endmodule

module Decoder16 (
  input  [15:0] Instr,
  input  Z,
  input  C,
  output [3:0] AluOp,
  output RegWrite,
  output [1:0] WSrc,
  output Jump,
  output FlagWrite,
  output OutWrite,
  output Halt
);

  wire jc, jmp, jnz, jz, ni12, ni13, ni14, ni15, nz, tc, tnz, tz;

  not not_1 (ni12, Instr[12]);
  not not_2 (ni13, Instr[13]);
  not not_3 (ni14, Instr[14]);
  not not_4 (ni15, Instr[15]);
  not not_5 (nz, Z);
  and and_1 (FlagWrite, ni12, ni13, ni14, ni15);
  and and_2 (WSrc[0], Instr[12], ni13, ni14, ni15);
  and and_3 (WSrc[1], ni12, Instr[13], ni14, ni15);
  and and_4 (jmp, Instr[12], Instr[13], ni14, ni15);
  and and_5 (jz, ni12, ni13, Instr[14], ni15);
  and and_6 (jnz, Instr[12], ni13, Instr[14], ni15);
  and and_7 (jc, ni12, Instr[13], Instr[14], ni15);
  and and_8 (OutWrite, Instr[12], Instr[13], Instr[14], ni15);
  and and_9 (Halt, ni12, ni13, ni14, Instr[15]);
  and and_10 (tz, jz, Z);
  and and_11 (tnz, jnz, nz);
  and and_12 (tc, jc, C);
  or or_1 (RegWrite, FlagWrite, WSrc[0], WSrc[1]);
  or or_2 (Jump, jmp, tz, tnz, tc);

  assign AluOp = Instr[3:0];

  // Other names for the same wires on the sheet: i0 = Instr[0]; i1 = Instr[1]; i2 = Instr[2]; i3 = Instr[3];
  //   i12 = Instr[12]; i13 = Instr[13]; i14 = Instr[14]; i15 = Instr[15]; ldi = WSrc[0]; mov = WSrc[1]
endmodule

module cpu (
  input  Reset,
  output [7:0] PC,
  output [7:0] R0,
  output [7:0] R1,
  output [7:0] R2,
  output [7:0] R3,
  output [7:0] Out,
  output Z,
  output C,
  output Halt
);

  wire ac, az, clk, dh_a, dh_a_on, dh_b, dh_b_on, dh_c, dh_c_on, dh_d, dh_d_on, dh_e, dh_e_on, dh_f, dh_f_on,
       dh_g, dh_g_on, do_a_on, do_b_on, do_c_on, do_d_on, do_e_on, do_f_on, do_g_on, dt_a, dt_a_on, dt_b,
       dt_b_on, dt_c, dt_c_on, dt_d, dt_d_on, dt_e, dt_e_on, dt_f, dt_f_on, dt_g, dt_g_on, fc, FlagWrite,
       fld, fz, hon, in8, in9, in10, in11, Jump, nreset, old, OutWrite, RegWrite, ton, ws0, ws1;
  wire [3:0] aluop, dh, \do , dt;
  wire [7:0] imm, od, qa, qb, r, w1, wd;
  wire [15:12] instr;

  Clock u_CLK (.out(clk));
  not not_1 (nreset, Reset);
  PC8 u_PC (.D(imm), .Jump(Jump), .Hold(Halt), .CLK(clk), .Reset(Reset), .Q(PC));
  ROM #(.addrWidth(8), .dataWidth(16)) Program (.addr(PC), .data({instr, in11, in10, in9, in8, imm}));
  Decoder16 decoder16_1 (
    .Instr({instr, in11, in10, in9, in8, imm}), .Z(Z), .C(C), .AluOp(aluop), .RegWrite(RegWrite),
    .WSrc({ws1, ws0}), .Jump(Jump), .FlagWrite(FlagWrite), .OutWrite(OutWrite), .Halt(Halt));
  RegFile4x8 regfile4x8_1 (
    .D(wd), .WSel({in11, in10}), .WE(RegWrite), .RSelA({in11, in10}), .RSelB({in9, in8}), .CLK(clk),
    .Reset(Reset), .QA(qa), .QB(qb), .R0(R0), .R1(R1), .R2(R2), .R3(R3));
  ALUCore8 alucore8_1 (.A(qa), .B(qb), .Op(aluop), .R(r), .Z(az), .C(ac));  // open: S, V
  Select8bit select8bit_1 (.Sel(ws0), .X(r), .Y(imm), .Out(w1));
  and and_1 (fz, az, nreset);
  and and_2 (fc, ac, nreset);
  or or_1 (fld, FlagWrite, Reset);
  or or_2 (old, OutWrite, Reset);
  Select8bit select8bit_2 (.Sel(Reset), .X(qb), .Y({8{1'b0}}), .Out(od));
  Select8bit select8bit_3 (.Sel(ws1), .X(w1), .Y(qb), .Out(wd));
  Register4bit Flags (.Load(fld), .D0(fz), .D1(fc), .D2(1'b0), .D3(1'b0), .CLK(clk), .Q0(Z), .Q1(C));  // open: Q2, Q3
  Register8bit Display (.Load(old), .D(od), .CLK(clk), .Q(Out));
  BinToBCD8 bintobcd8_1 (.In(Out), .Hundreds(dh), .Tens(dt), .Ones(\do ));
  or or_3 (hon, dh[0], dh[1], dh[2], dh[3]);
  or or_4 (ton, hon, dt[0], dt[1], dt[2], dt[3]);
  HexDecoder7 hexdecoder7_1 (.In(dh), .a(dh_a), .b(dh_b), .c(dh_c), .d(dh_d), .e(dh_e), .f(dh_f), .g(dh_g));
  HexDecoder7 hexdecoder7_2 (.In(dt), .a(dt_a), .b(dt_b), .c(dt_c), .d(dt_d), .e(dt_e), .f(dt_f), .g(dt_g));
  HexDecoder7 hexdecoder7_3 (
    .In(\do ), .a(do_a_on), .b(do_b_on), .c(do_c_on), .d(do_d_on), .e(do_e_on), .f(do_f_on), .g(do_g_on));
  and and_3 (dh_a_on, dh_a, hon);
  and and_4 (dh_b_on, dh_b, hon);
  and and_5 (dh_c_on, dh_c, hon);
  and and_6 (dh_d_on, dh_d, hon);
  and and_7 (dh_e_on, dh_e, hon);
  and and_8 (dh_f_on, dh_f, hon);
  and and_9 (dh_g_on, dh_g, hon);
  and and_10 (dt_a_on, dt_a, ton);
  and and_11 (dt_b_on, dt_b, ton);
  and and_12 (dt_c_on, dt_c, ton);
  and and_13 (dt_d_on, dt_d, ton);
  and and_14 (dt_e_on, dt_e, ton);
  and and_15 (dt_f_on, dt_f, ton);
  and and_16 (dt_g_on, dt_g, ton);
  _7_Segment_Display u_7_segment_display_1 (
    .g(dh_g_on), .f(dh_f_on), .a(dh_a_on), .b(dh_b_on), .e(dh_e_on), .d(dh_d_on), .c(dh_c_on));  // open: dp
  _7_Segment_Display u_7_segment_display_2 (
    .g(dt_g_on), .f(dt_f_on), .a(dt_a_on), .b(dt_b_on), .e(dt_e_on), .d(dt_d_on), .c(dt_c_on));  // open: dp
  _7_Segment_Display u_7_segment_display_3 (
    .g(do_g_on), .f(do_f_on), .a(do_a_on), .b(do_b_on), .e(do_e_on), .d(do_d_on), .c(do_c_on));  // open: dp
  LED HaltLed (.in(Halt));
  LED ZLed (.in(Z));
  LED CLed (.in(C));

  // Other names for the same wires on the sheet: in0 = imm[0]; instr[11:0] = {in11, in10, in9, in8, imm};
  //   in1 = imm[1]; in2 = imm[2]; in3 = imm[3]; in4 = imm[4]; in5 = imm[5]; in6 = imm[6]; in7 = imm[7];
  //   rd[1:0] = {in11, in10}; rs[1:0] = {in9, in8}; wsrc[1:0] = {ws1, ws0}

  // Notes on the sheet:
  //   contents of Program (hex, n*v repeats v):
  //   1000 1401 7000 2800 900 6009 2100 2600 3002 7100 8000
endmodule
