// Logisim project ALU.circ as structural Verilog: 18 circuits, main circuit main
module main (
  input  A0,
  input  A1,
  input  A2,
  input  A3,
  input  Execute,
  input  Load,
  input  Op0,
  input  Op1,
  input  Op2,
  input  Op3,
  input  B0,
  input  B1,
  input  B2,
  input  B3,
  input  Reset,
  output State0,
  output State1
);

  wire alucore_1_cout, alucore_1_r0, alucore_1_r1, alucore_1_r2, alucore_1_r3, Clk_out, nor_1_out,
       OutputRegister_q0, OutputRegister_q1, OutputRegister_q2, OutputRegister_q3, RegisterA_q0,
       RegisterA_q1, RegisterA_q2, RegisterA_q3, RegisterB_q0, RegisterB_q1, RegisterB_q2, RegisterB_q3,
       sevensegment_1_a, sevensegment_1_b, sevensegment_1_c, sevensegment_1_d, sevensegment_1_e,
       sevensegment_1_f, sevensegment_1_g;

  Clock Clk (.out(Clk_out));
  Register4bit RegisterA (
    .Load(Load), .D0(A0), .D1(A1), .D2(A2), .D3(A3), .CLK(Clk_out), .Q0(RegisterA_q0), .Q1(RegisterA_q1),
    .Q2(RegisterA_q2), .Q3(RegisterA_q3));
  Register4bit RegisterB (
    .Load(Load), .D0(B0), .D1(B1), .D2(B2), .D3(B3), .CLK(Clk_out), .Q0(RegisterB_q0), .Q1(RegisterB_q1),
    .Q2(RegisterB_q2), .Q3(RegisterB_q3));
  ALUCore alucore_1 (
    .A0(RegisterA_q0), .A2(RegisterA_q2), .A3(RegisterA_q3), .A1(RegisterA_q1), .B0(RegisterB_q0),
    .B1(RegisterB_q1), .B2(RegisterB_q2), .B3(RegisterB_q3), .Op0(Op0), .Op1(Op1), .Op2(Op2), .Op3(Op3),
    .Cout(alucore_1_cout), .R0(alucore_1_r0), .R1(alucore_1_r1), .R2(alucore_1_r2), .R3(alucore_1_r3));
  ControlUnit controlunit_1 (.EXECUTE(Execute), .Load(Load), .Reset(Reset), .S0(State0), .S1(State1));
  LED CFlagLed (.in(alucore_1_cout));
  Register4bit OutputRegister (
    .Load(Execute), .D0(alucore_1_r0), .D1(alucore_1_r1), .D2(alucore_1_r2), .D3(alucore_1_r3),
    .CLK(Clk_out), .Q0(OutputRegister_q0), .Q1(OutputRegister_q1), .Q2(OutputRegister_q2),
    .Q3(OutputRegister_q3));
  LED SFlagLed (.in(OutputRegister_q3));
  nor nor_1 (nor_1_out, OutputRegister_q0, OutputRegister_q1, OutputRegister_q2, OutputRegister_q3);
  LED ZLed (.in(nor_1_out));
  SevenSegment sevensegment_1 (
    .R3(OutputRegister_q3), .R2(OutputRegister_q2), .R1(OutputRegister_q1), .R0(OutputRegister_q0),
    .a(sevensegment_1_a), .b(sevensegment_1_b), .c(sevensegment_1_c), .e(sevensegment_1_e),
    .d(sevensegment_1_d), .f(sevensegment_1_f), .g(sevensegment_1_g));
  _7_Segment_Display u_7_segment_display_1 (
    .g(sevensegment_1_g), .f(sevensegment_1_f), .a(sevensegment_1_a), .b(sevensegment_1_b),
    .e(sevensegment_1_e), .d(sevensegment_1_d), .c(sevensegment_1_c));  // open: dp
endmodule

module HalfAdder (
  input  A,
  input  B,
  output Sum,
  output Carry
);

  and and_1 (Carry, A, B);
  xor xor_1 (Sum, A, B);
endmodule

module FullAdder (
  input  A,
  input  B,
  input  Cin,
  output Sum,
  output Cout
);

  wire halfadder_1_carry, halfadder_1_sum, halfadder_2_carry;

  HalfAdder halfadder_1 (.A(A), .B(B), .Sum(halfadder_1_sum), .Carry(halfadder_1_carry));
  HalfAdder halfadder_2 (.A(halfadder_1_sum), .B(Cin), .Sum(Sum), .Carry(halfadder_2_carry));
  or or_1 (Cout, halfadder_1_carry, halfadder_2_carry);
endmodule

module Adder4bit (
  input  A1,
  input  A3,
  input  A2,
  input  B1,
  input  B3,
  input  B2,
  input  A0,
  input  B0,
  input  Cin,
  output S1,
  output S2,
  output S0,
  output S3,
  output Cout
);

  wire fulladder_1_cout, fulladder_2_cout, fulladder_3_cout;

  FullAdder fulladder_1 (.A(A0), .B(B0), .Cin(Cin), .Sum(S0), .Cout(fulladder_1_cout));
  FullAdder fulladder_2 (.A(A1), .B(B1), .Cin(fulladder_1_cout), .Sum(S1), .Cout(fulladder_2_cout));
  FullAdder fulladder_3 (.A(A2), .B(B2), .Cin(fulladder_2_cout), .Sum(S2), .Cout(fulladder_3_cout));
  FullAdder fulladder_4 (.A(A3), .B(B3), .Cin(fulladder_3_cout), .Sum(S3), .Cout(Cout));
endmodule

module Subtractor4bit (
  input  A1,
  input  A3,
  input  A2,
  input  B1,
  input  B3,
  input  B2,
  input  A0,
  input  B0,
  output S1,
  output S2,
  output S0,
  output S3,
  output Cout
);

  wire not_1_out, not_2_out, not_3_out, not_4_out;

  not not_1 (not_1_out, B1);
  not not_2 (not_2_out, B3);
  not not_3 (not_3_out, B2);
  not not_4 (not_4_out, B0);
  Adder4bit adder4bit_1 (
    .A1(A1), .A3(A3), .A2(A2), .B1(not_1_out), .B3(not_2_out), .B2(not_3_out), .A0(A0), .B0(not_4_out),
    .Cin(1'b1), .S1(S1), .S2(S2), .S0(S0), .S3(S3), .Cout(Cout));
endmodule

module INC4bit (
  input  A1,
  input  A3,
  input  A2,
  input  A0,
  output S1,
  output S2,
  output S0,
  output S3,
  output Cout
);

  Adder4bit adder4bit_1 (
    .A1(A1), .A3(A3), .A2(A2), .B1(1'b0), .B3(1'b0), .B2(1'b0), .A0(A0), .B0(1'b0), .Cin(1'b1), .S1(S1),
    .S2(S2), .S0(S0), .S3(S3), .Cout(Cout));
endmodule

module DEC4bit (
  input  A1,
  input  A3,
  input  A2,
  input  A0,
  output S1,
  output S2,
  output S0,
  output S3,
  output Cout
);

  Adder4bit adder4bit_1 (
    .A1(A1), .A3(A3), .A2(A2), .B1(1'b1), .B3(1'b1), .B2(1'b1), .A0(A0), .B0(1'b1), .Cin(1'b0), .S1(S1),
    .S2(S2), .S0(S0), .S3(S3), .Cout(Cout));
endmodule

module LogicUnit (
  input  A3,
  input  A2,
  input  A1,
  input  A0,
  input  B0,
  input  B1,
  input  B2,
  input  B3,
  output NotA3,
  output NotA2,
  output NotA1,
  output NotA0,
  output And0,
  output Or0,
  output XOR0,
  output And1,
  output Or1,
  output XOR1,
  output And2,
  output Or2,
  output XOR2,
  output And3,
  output Or3,
  output XOR3
);

  not not_1 (NotA3, A3);
  not not_2 (NotA2, A2);
  not not_3 (NotA1, A1);
  not not_4 (NotA0, A0);
  and and_1 (And0, A0, B0);
  and and_2 (And1, A1, B1);
  and and_3 (And2, A2, B2);
  and and_4 (And3, A3, B3);
  or or_1 (Or0, A0, B0);
  or or_2 (Or1, A1, B1);
  or or_3 (Or2, A2, B2);
  or or_4 (Or3, A3, B3);
  xor xor_1 (XOR0, A0, B0);
  xor xor_2 (XOR1, A1, B1);
  xor xor_3 (XOR2, A2, B2);
  xor xor_4 (XOR3, A3, B3);
endmodule

module Register4bit (
  input  Load,
  input  D0,
  input  D1,
  input  D2,
  input  D3,
  input  CLK,
  output Q0,
  output Q1,
  output Q2,
  output Q3
);

  wire and_1_out, and_2_out, and_3_out, and_4_out, and_5_out, and_6_out, and_7_out, and_8_out, not_1_out,
       or_1_out, or_2_out, or_3_out, or_4_out;

  or or_1 (or_1_out, and_1_out, and_2_out);
  D_Flip_Flop d_ff_1 (.D(or_1_out), .clk(CLK), .Q(Q0));  // open: Qn, preset, reset
  and and_1 (and_1_out, not_1_out, Q0);
  and and_2 (and_2_out, Load, D0);
  or or_2 (or_2_out, and_3_out, and_4_out);
  and and_3 (and_3_out, not_1_out, Q1);
  and and_4 (and_4_out, Load, D1);
  D_Flip_Flop d_ff_2 (.D(or_2_out), .clk(CLK), .Q(Q1));  // open: Qn, preset, reset
  not not_1 (not_1_out, Load);
  D_Flip_Flop d_ff_3 (.D(or_3_out), .clk(CLK), .Q(Q2));  // open: Qn, preset, reset
  and and_5 (and_5_out, Load, D2);
  and and_6 (and_6_out, not_1_out, Q2);
  D_Flip_Flop d_ff_4 (.D(or_4_out), .clk(CLK), .Q(Q3));  // open: Qn, preset, reset
  or or_3 (or_3_out, and_6_out, and_5_out);
  and and_7 (and_7_out, Load, D3);
  and and_8 (and_8_out, not_1_out, Q3);
  or or_4 (or_4_out, and_8_out, and_7_out);
endmodule

module ALUCore (
  input  A0,
  input  A2,
  input  A3,
  input  A1,
  input  B0,
  input  B1,
  input  B2,
  input  B3,
  input  Op0,
  input  Op1,
  input  Op2,
  input  Op3,
  output Cout,
  output R0,
  output R1,
  output R2,
  output R3
);

  wire logicunit_1_nota0, logicunit_1_nota1, logicunit_1_nota2, logicunit_1_nota3;
  wire [3:0] adder4bit_1_s0, dec4bit_1_s0, div4bit_1_q0, inc4bit_1_s0, logicunit_1_and0, logicunit_1_or0,
       logicunit_1_xor0, multiplexer_1_out, subtractor4bit_1_s0;

  Multiplexer #(.select(3), .width(4)) multiplexer_1 (
    .in0(adder4bit_1_s0), .in1(subtractor4bit_1_s0), .in2(inc4bit_1_s0), .in3(dec4bit_1_s0),
    .in4(div4bit_1_q0), .in5(logicunit_1_and0), .in6(logicunit_1_or0), .in7(logicunit_1_xor0),
    .out(multiplexer_1_out), .sel({Op2, Op1, Op0}));
  Multiplexer multiplexer_2 (.in0(multiplexer_1_out[0]), .in1(logicunit_1_nota0), .out(R0), .sel(Op3));
  Multiplexer multiplexer_3 (.in0(multiplexer_1_out[1]), .in1(logicunit_1_nota1), .out(R1), .sel(Op3));
  Multiplexer multiplexer_4 (.in0(multiplexer_1_out[2]), .in1(logicunit_1_nota2), .out(R2), .sel(Op3));
  Multiplexer multiplexer_5 (.in0(multiplexer_1_out[3]), .in1(logicunit_1_nota3), .out(R3), .sel(Op3));
  Adder4bit adder4bit_1 (
    .A1(A1), .A3(A3), .A2(A2), .B1(B1), .B3(B3), .B2(B2), .A0(A0), .B0(B0), .S1(adder4bit_1_s0[1]),
    .S2(adder4bit_1_s0[2]), .S0(adder4bit_1_s0[0]), .S3(adder4bit_1_s0[3]), .Cout(Cout));  // open: Cin
  DIV4bit div4bit_1 (
    .A3(A3), .A2(A2), .A1(A1), .A0(A0), .B3(B3), .B2(B2), .B1(B1), .B0(B0), .Q3(div4bit_1_q0[3]),
    .Q2(div4bit_1_q0[2]), .Q1(div4bit_1_q0[1]), .Q0(div4bit_1_q0[0]));  // open: R3, R2, R1, R0
  LogicUnit logicunit_1 (
    .A3(A3), .A2(A2), .A1(A1), .A0(A0), .B0(B0), .B1(B1), .B2(B2), .B3(B3), .NotA3(logicunit_1_nota3),
    .NotA2(logicunit_1_nota2), .NotA1(logicunit_1_nota1), .NotA0(logicunit_1_nota0),
    .And0(logicunit_1_and0[0]), .Or0(logicunit_1_or0[0]), .XOR0(logicunit_1_xor0[0]),
    .And1(logicunit_1_and0[1]), .Or1(logicunit_1_or0[1]), .XOR1(logicunit_1_xor0[1]),
    .And2(logicunit_1_and0[2]), .Or2(logicunit_1_or0[2]), .XOR2(logicunit_1_xor0[2]),
    .And3(logicunit_1_and0[3]), .Or3(logicunit_1_or0[3]), .XOR3(logicunit_1_xor0[3]));
  Subtractor4bit subtractor4bit_1 (
    .A1(A1), .A3(A3), .A2(A2), .B1(B1), .B3(B3), .B2(B2), .A0(A0), .B0(B0), .S1(subtractor4bit_1_s0[1]),
    .S2(subtractor4bit_1_s0[2]), .S0(subtractor4bit_1_s0[0]), .S3(subtractor4bit_1_s0[3]));  // open: Cout
  INC4bit inc4bit_1 (
    .A1(A1), .A3(A3), .A2(A2), .A0(A0), .S1(inc4bit_1_s0[1]), .S2(inc4bit_1_s0[2]), .S0(inc4bit_1_s0[0]),
    .S3(inc4bit_1_s0[3]));  // open: Cout
  DEC4bit dec4bit_1 (
    .A1(A1), .A3(A3), .A2(A2), .A0(A0), .S1(dec4bit_1_s0[1]), .S2(dec4bit_1_s0[2]), .S0(dec4bit_1_s0[0]),
    .S3(dec4bit_1_s0[3]));  // open: Cout
endmodule

module ControlUnit (
  input  EXECUTE,
  input  Load,
  input  Reset,
  output S0,
  output S1
);

  wire A_out, B_out, C_out, CLK_out, D_out, DISPLAYLED_out, E_out, EXECUTELED_out, IdleLed_out, LoadLed_out,
       not_1_out, not_2_out, not_3_out, or_1_out, or_2_out;

  Clock CLK (.out(CLK_out));
  D_Flip_Flop d_ff_1 (.D(or_1_out), .clk(CLK_out), .Q(S0), .reset(Reset));  // open: Qn, preset
  D_Flip_Flop d_ff_2 (.D(or_2_out), .clk(CLK_out), .Q(S1), .reset(Reset));  // open: Qn, preset
  not not_1 (not_1_out, EXECUTE);
  not not_2 (not_2_out, S0);
  not not_3 (not_3_out, S1);
  and B (B_out, not_2_out, S1);
  and D (D_out, not_3_out, EXECUTE, S0);
  and E (E_out, S1, not_2_out);
  and C (C_out, not_3_out, S0, not_1_out);
  and A (A_out, not_2_out, Load, not_3_out);
  or or_1 (or_1_out, A_out, C_out, B_out);
  or or_2 (or_2_out, D_out, E_out);
  and IdleLed (IdleLed_out, not_2_out, not_3_out);
  and LoadLed (LoadLed_out, not_3_out, S0);
  and EXECUTELED (EXECUTELED_out, not_2_out, S1);
  and DISPLAYLED (DISPLAYLED_out, S1, S0);
  LED led_1 (.in(IdleLed_out));
  LED led_2 (.in(LoadLed_out));
  LED led_3 (.in(EXECUTELED_out));
  LED led_4 (.in(DISPLAYLED_out));
endmodule

module SevenSegment (
  input  R3,
  input  R2,
  input  R1,
  input  R0,
  output a,
  output b,
  output c,
  output e,
  output d,
  output f,
  output g
);

  wire And1_out, And2_out, And3_out, And4_out, And5_out, And6_out, bAnd1_out, bAnd2_out, bAnd3_out,
       bAnd4_out, bAnd5_out, C1_out, C2_out, C3_out, C4_out, C5_out, D1_out, D2_out, D3_out, D4_out, D5_out,
       E1_out, E2_out, E3_out, E4_out, F1_out, F2_out, F3_out, F4_out, F5_out, G1_out, G2_out, G3_out,
       G4_out, G5_out, not_1_out, not_2_out, not_3_out, not_4_out, or_1_out, or_2_out, or_7_out, or_8_out;

  not not_1 (not_1_out, R3);
  not not_2 (not_2_out, R2);
  not not_3 (not_3_out, R1);
  not not_4 (not_4_out, R0);
  and And1 (And1_out, R1, R2);
  and And2 (And2_out, R1, not_1_out);
  and And3 (And3_out, R3, not_4_out);
  and And4 (And4_out, not_2_out, not_4_out);
  and And5 (And5_out, not_1_out, R2, R0);
  and And6 (And6_out, R3, not_3_out, not_2_out);
  and E1 (E1_out, not_4_out, not_2_out);
  and E2 (E2_out, not_4_out, R1);
  and E3 (E3_out, R3, R1);
  and E4 (E4_out, R3, R2);
  and F1 (F1_out, R2, not_4_out);
  and F2 (F2_out, R2, not_3_out);
  and F3 (F3_out, R3, not_2_out);
  and F4 (F4_out, R3, R1);
  and F5 (F5_out, not_4_out, not_3_out, not_1_out);
  and G1 (G1_out, R0, R3);
  and G2 (G2_out, R1, R0);
  and G3 (G3_out, R1, not_2_out);
  and G4 (G4_out, R3, not_2_out);
  and G5 (G5_out, R2, not_3_out, not_1_out);
  or or_1 (or_1_out, And1_out, And2_out, And3_out);
  or or_2 (or_2_out, And4_out, And5_out, And6_out);
  or or_3 (e, E1_out, E2_out, E3_out, E4_out);
  or or_4 (f, F1_out, F2_out, F3_out, F4_out, F5_out);
  or or_5 (g, G1_out, G2_out, G3_out, G4_out, G5_out);
  or or_6 (a, or_1_out, or_2_out);
  and C1 (C1_out, R0, not_3_out);
  and C2 (C2_out, R0, not_1_out);
  and C3 (C3_out, R2, not_1_out);
  and C4 (C4_out, R3, not_2_out);
  and C5 (C5_out, not_3_out, not_1_out);
  and D1 (D1_out, R3, not_3_out);
  and D2 (D2_out, R0, R1, not_2_out);
  and D3 (D3_out, R0, R2, not_3_out);
  and D4 (D4_out, R1, R2, not_4_out);
  and D5 (D5_out, not_4_out, not_2_out, not_1_out);
  and bAnd1 (bAnd1_out, not_4_out, not_2_out);
  and bAnd2 (bAnd2_out, not_2_out, not_1_out);
  and bAnd3 (bAnd3_out, R0, R1, not_1_out);
  and bAnd4 (bAnd4_out, R0, R3, not_3_out);
  and bAnd5 (bAnd5_out, not_4_out, not_3_out, not_1_out);
  or or_7 (or_7_out, C1_out, C2_out, C3_out);
  or or_8 (or_8_out, C4_out, C5_out);
  or or_9 (d, D1_out, D2_out, D3_out, D4_out, D5_out);
  or or_10 (b, bAnd1_out, bAnd2_out, bAnd3_out, bAnd4_out, bAnd5_out);
  or or_11 (c, or_7_out, or_8_out);
endmodule

module DIV4bit (
  input  A3,
  input  A2,
  input  A1,
  input  A0,
  input  B3,
  input  B2,
  input  B1,
  input  B0,
  output R3,
  output R2,
  output R1,
  output R0,
  output Q3,
  output Q2,
  output Q1,
  output Q0
);

  wire Step1_n0, Step1_n1, Step1_n2, Step1_qout0, Step1_qout1, Step1_qout2, Step1_qout3, Step2_n0, Step2_n1,
       Step2_n2, Step2_qout0, Step2_qout1, Step2_qout2, Step2_qout3, Step3_n0, Step3_n1, Step3_n2,
       Step3_qout0, Step3_qout1, Step3_qout2, Step3_qout3;

  DivStepFull Step3 (
    .R3(1'b0), .R2(1'b0), .R1(1'b0), .R0(A3), .B3(B3), .B2(B2), .B1(B1), .B0(B0), .Qin3(1'b0), .Qin2(1'b0),
    .Qin1(1'b0), .Qin0(1'b0), .N2(Step3_n2), .N1(Step3_n1), .N0(Step3_n0), .Qout3(Step3_qout3),
    .Qout2(Step3_qout2), .Qout1(Step3_qout1), .Qout0(Step3_qout0));  // open: N3
  DivStepFull Step2 (
    .R3(Step3_n2), .R2(Step3_n1), .R1(Step3_n0), .R0(A2), .B3(B3), .B2(B2), .B1(B1), .B0(B0),
    .Qin3(Step3_qout3), .Qin2(Step3_qout2), .Qin1(Step3_qout1), .Qin0(Step3_qout0), .N2(Step2_n2),
    .N1(Step2_n1), .N0(Step2_n0), .Qout3(Step2_qout3), .Qout2(Step2_qout2), .Qout1(Step2_qout1),
    .Qout0(Step2_qout0));  // open: N3
  DivStepFull Step1 (
    .R3(Step2_n2), .R2(Step2_n1), .R1(Step2_n0), .R0(A1), .B3(B3), .B2(B2), .B1(B1), .B0(B0),
    .Qin3(Step2_qout3), .Qin2(Step2_qout2), .Qin1(Step2_qout1), .Qin0(Step2_qout0), .N2(Step1_n2),
    .N1(Step1_n1), .N0(Step1_n0), .Qout3(Step1_qout3), .Qout2(Step1_qout2), .Qout1(Step1_qout1),
    .Qout0(Step1_qout0));  // open: N3
  DivStepFull Step0 (
    .R3(Step1_n2), .R2(Step1_n1), .R1(Step1_n0), .R0(A0), .B3(B3), .B2(B2), .B1(B1), .B0(B0),
    .Qin3(Step1_qout3), .Qin2(Step1_qout2), .Qin1(Step1_qout1), .Qin0(Step1_qout0), .N3(R3), .N2(R2),
    .N1(R1), .N0(R0), .Qout3(Q3), .Qout2(Q2), .Qout1(Q1), .Qout0(Q0));
endmodule

module Comparator4bit (
  input  A3,
  input  A2,
  input  A1,
  input  A0,
  input  B3,
  input  B2,
  input  B1,
  input  B0,
  output GTE
);

  wire E0_out, E1_out, E2_out, E3_out, EQ_out, G0_out, G1_out, G2_out, G3_out, not_1_out, not_2_out,
       not_3_out, not_4_out;

  not not_1 (not_1_out, B3);
  not not_2 (not_2_out, B2);
  not not_3 (not_3_out, B1);
  not not_4 (not_4_out, B0);
  xnor E3 (E3_out, A3, B3);
  xnor E2 (E2_out, A2, B2);
  xnor E1 (E1_out, A1, B1);
  xnor E0 (E0_out, A0, B0);
  and G3 (G3_out, A3, not_1_out);
  and G2 (G2_out, E3_out, A2, not_2_out);
  and G1 (G1_out, E3_out, E2_out, A1, not_3_out);
  and G0 (G0_out, E3_out, E2_out, E1_out, A0, not_4_out);
  and EQ (EQ_out, E3_out, E2_out, E1_out, E0_out);
  or or_1 (GTE, G3_out, G2_out, G1_out, G0_out, EQ_out);
endmodule

module Select1bit (
  input  Sel,
  input  X,
  input  Y,
  output SelOut
);

  wire and_1_out, and_2_out, not_1_out;

  not not_1 (not_1_out, Sel);
  and and_1 (and_1_out, not_1_out, X);
  and and_2 (and_2_out, Sel, Y);
  or or_1 (SelOut, and_1_out, and_2_out);
endmodule

module Select4bit (
  input  Sel,
  input  X3,
  input  X2,
  input  X1,
  input  X0,
  input  Y3,
  input  Y2,
  input  Y1,
  input  Y0,
  output Out03,
  output Out02,
  output Out01,
  output Out00
);

  Select1bit select1bit_1 (.Sel(Sel), .X(X3), .Y(Y3), .SelOut(Out03));
  Select1bit select1bit_2 (.Sel(Sel), .X(X2), .Y(Y2), .SelOut(Out02));
  Select1bit select1bit_3 (.Sel(Sel), .X(X1), .Y(Y1), .SelOut(Out01));
  Select1bit select1bit_4 (.Sel(Sel), .X(X0), .Y(Y0), .SelOut(Out00));
endmodule

module DivStep (
  input  R3,
  input  R2,
  input  R1,
  input  R0,
  input  B3,
  input  B2,
  input  B1,
  input  B0,
  output Q,
  output N3,
  output N2,
  output N1,
  output N0
);

  wire subtractor4bit_1_s0, subtractor4bit_1_s1, subtractor4bit_1_s2, subtractor4bit_1_s3;

  Comparator4bit comparator4bit_1 (.A3(R3), .A2(R2), .A1(R1), .A0(R0), .B3(B3), .B2(B2), .B1(B1), .B0(B0), .GTE(Q));
  Subtractor4bit subtractor4bit_1 (
    .A1(R1), .A3(R3), .A2(R2), .B1(B1), .B3(B3), .B2(B2), .A0(R0), .B0(B0), .S1(subtractor4bit_1_s1),
    .S2(subtractor4bit_1_s2), .S0(subtractor4bit_1_s0), .S3(subtractor4bit_1_s3));  // open: Cout
  Select4bit select4bit_1 (
    .Sel(Q), .X3(R3), .X2(R2), .X1(R1), .X0(R0), .Y3(subtractor4bit_1_s3), .Y2(subtractor4bit_1_s2),
    .Y1(subtractor4bit_1_s1), .Y0(subtractor4bit_1_s0), .Out03(N3), .Out02(N2), .Out01(N1), .Out00(N0));
endmodule

module DivStepFull (
  input  R3,
  input  R2,
  input  R1,
  input  R0,
  input  B3,
  input  B2,
  input  B1,
  input  B0,
  input  Qin3,
  input  Qin2,
  input  Qin1,
  input  Qin0,
  output N3,
  output N2,
  output N1,
  output N0,
  output Qout3,
  output Qout2,
  output Qout1,
  output Qout0
);

  wire comparator4bit_1_gte, or_1_out, subtractor4bit_1_s0, subtractor4bit_1_s1, subtractor4bit_1_s2,
       subtractor4bit_1_s3;

  or or_1 (or_1_out, B3, B2, B1, B0);
  Comparator4bit comparator4bit_1 (
    .A3(R3), .A2(R2), .A1(R1), .A0(R0), .B3(B3), .B2(B2), .B1(B1), .B0(B0), .GTE(comparator4bit_1_gte));
  Subtractor4bit subtractor4bit_1 (
    .A1(R1), .A3(R3), .A2(R2), .B1(B1), .B3(B3), .B2(B2), .A0(R0), .B0(B0), .S1(subtractor4bit_1_s1),
    .S2(subtractor4bit_1_s2), .S0(subtractor4bit_1_s0), .S3(subtractor4bit_1_s3));  // open: Cout
  and canSubstract (Qout0, comparator4bit_1_gte, or_1_out);
  Select4bit select4bit_1 (
    .Sel(Qout0), .X3(R3), .X2(R2), .X1(R1), .X0(R0), .Y3(subtractor4bit_1_s3), .Y2(subtractor4bit_1_s2),
    .Y1(subtractor4bit_1_s1), .Y0(subtractor4bit_1_s0), .Out03(N3), .Out02(N2), .Out01(N1), .Out00(N0));

  assign Qout1 = Qin0;
  assign Qout2 = Qin1;
  assign Qout3 = Qin2;
endmodule
